// Logisim project cs.circ as structural Verilog: 2 circuits, main circuit main
module main (
  input  I,
  input  M,
  input  R,
  input  L,
  output C
);

  wire and_1_out, and_2_out, not_1_out;

  not not_1 (not_1_out, M);
  and and_1 (and_1_out, I, not_1_out);
  and and_2 (and_2_out, not_1_out, R, L);
  or or_1 (C, and_1_out, and_2_out);
endmodule

module _15 (
  input  in_1,
  input  in_2,
  input  in_3,
  input  in_4,
  input  M,
  input  N,
  output _1,
  output _2,
  output _3,
  output _4,
  output _5,
  output _6,
  output out_13,
  output g
);

  wire and_1_out, and_2_out, and_3_out, and_4_out, and_5_out, and_6_out, and_7_out, and_8_out, not_1_out,
       not_2_out, not_3_out, not_4_out, not_6_out, not_7_out, not_14_out, or_1_out, or_2_out, or_3_out,
       or_4_out, or_5_out, or_6_out;

  not not_1 (not_1_out, in_1);
  not not_2 (not_2_out, in_2);
  not not_3 (not_3_out, in_3);
  not not_4 (not_4_out, in_4);
  or or_1 (or_1_out, M, ~N);  // OR_Gate
  or or_2 (or_2_out, ~M, N);  // OR_Gate
  and and_1 (and_1_out, not_2_out, in_3);
  or or_3 (or_3_out, in_2, not_3_out);
  not not_5 (g, and_2_out);
  and and_2 (and_2_out, or_1_out, or_2_out);
  or or_4 (or_4_out, not_1_out, and_1_out);
  and and_3 (and_3_out, in_1, in_2, not_3_out, not_4_out);
  or or_5 (or_5_out, in_1, not_2_out);
  and and_4 (and_4_out, not_1_out, not_2_out);
  or or_6 (or_6_out, not_1_out, not_3_out, not_4_out);
  not not_6 (not_6_out, or_3_out);
  and and_5 (and_5_out, not_6_out, in_1, in_4);
  and and_6 (and_6_out, in_1, in_2);
  not not_7 (not_7_out, and_6_out);
  not not_8 (_1, or_4_out);
  not not_9 (_2, and_3_out);
  not not_10 (_3, or_5_out);
  not not_11 (_4, and_4_out);
  not not_12 (_5, or_6_out);
  not not_13 (_6, and_5_out);
  and and_7 (and_7_out, not_7_out, in_3);
  not not_14 (not_14_out, and_7_out);
  and and_8 (and_8_out, not_14_out, in_4);
  not not_15 (out_13, and_8_out);
endmodule
