// Logisim project Lab4 - Memory.circ as structural Verilog: 1 circuit, main circuit Direct Mapped Cache
module Direct_Mapped_Cache (
  input  [15:0] ByteAddress,
  input  [31:0] BlockDataInput,
  input  BlockDataReady,
  input  CLK,
  output [7:0] DataOutput,
  output Miss
);

  wire comparator_1_eq, demultiplexer_1_out0, demultiplexer_1_out1, demultiplexer_1_out2,
       demultiplexer_1_out3, demultiplexer_1_out4, demultiplexer_1_out5, demultiplexer_1_out6,
       demultiplexer_1_out7, demultiplexer_2_out0, demultiplexer_2_out1, demultiplexer_2_out2,
       demultiplexer_2_out3, demultiplexer_2_out4, demultiplexer_2_out5, demultiplexer_2_out6,
       demultiplexer_2_out7, Reset;
  wire [7:0] controlled_buffer_1_out, controlled_buffer_1_out_2, controlled_buffer_1_out_3,
       controlled_buffer_1_out_4;
  wire [10:0] register_11_q, register_14_q, register_17_q;
  wire [11:0] multiplexer_2_out, register_2_q, register_5_q, register_8_q, register_20_q, register_23_q;
  wire [11:11] register_10_q, register_13_q, register_16_q;
  wire [31:0] register_3_q, register_6_q, register_9_q, register_12_q, register_15_q, register_18_q,
       register_21_q, register_24_q;

  Demultiplexer #(.select(3), .enable("false")) demultiplexer_1 (
    .out0(demultiplexer_1_out0), .out1(demultiplexer_1_out1), .out2(demultiplexer_1_out2),
    .out3(demultiplexer_1_out3), .out4(demultiplexer_1_out4), .out5(demultiplexer_1_out5),
    .out6(demultiplexer_1_out6), .out7(demultiplexer_1_out7), .in(BlockDataReady), .sel(ByteAddress[4:2]));
  Register #(.width(1)) register_1 (.D(1'b1), .en(demultiplexer_1_out7), .Q(register_2_q[11]), .clk(CLK), .clr(Reset));
  Register #(.width(11)) register_2 (
    .D(ByteAddress[15:5]), .en(demultiplexer_1_out7), .Q(register_2_q[10:0]), .clk(CLK), .clr(Reset));
  Register #(.width(32)) register_3 (
    .D(BlockDataInput), .en(demultiplexer_1_out7), .Q(register_3_q), .clk(CLK), .clr(Reset));
  assign {controlled_buffer_1_out_4, controlled_buffer_1_out_3, controlled_buffer_1_out_2, controlled_buffer_1_out} = demultiplexer_2_out7 ? register_3_q : 32'bz;  // Controlled_Buffer controlled_buffer_1
  Button u_Reset (.out(Reset));
  Register #(.width(1)) register_4 (.D(1'b1), .en(demultiplexer_1_out6), .Q(register_5_q[11]), .clk(CLK), .clr(Reset));
  Register #(.width(11)) register_5 (
    .D(ByteAddress[15:5]), .en(demultiplexer_1_out6), .Q(register_5_q[10:0]), .clk(CLK), .clr(Reset));
  Register #(.width(32)) register_6 (
    .D(BlockDataInput), .en(demultiplexer_1_out6), .Q(register_6_q), .clk(CLK), .clr(Reset));
  Register #(.width(1)) register_7 (.D(1'b1), .en(demultiplexer_1_out5), .Q(register_8_q[11]), .clk(CLK), .clr(Reset));
  Register #(.width(11)) register_8 (
    .D(ByteAddress[15:5]), .en(demultiplexer_1_out5), .Q(register_8_q[10:0]), .clk(CLK), .clr(Reset));
  assign {controlled_buffer_1_out_4, controlled_buffer_1_out_3, controlled_buffer_1_out_2, controlled_buffer_1_out} = demultiplexer_2_out6 ? register_6_q : 32'bz;  // Controlled_Buffer controlled_buffer_2
  Register #(.width(32)) register_9 (
    .D(BlockDataInput), .en(demultiplexer_1_out5), .Q(register_9_q), .clk(CLK), .clr(Reset));
  assign {controlled_buffer_1_out_4, controlled_buffer_1_out_3, controlled_buffer_1_out_2, controlled_buffer_1_out} = demultiplexer_2_out5 ? register_9_q : 32'bz;  // Controlled_Buffer controlled_buffer_3
  Register #(.width(1)) register_10 (
    .D(1'b1), .en(demultiplexer_1_out4), .Q(register_10_q[11]), .clk(CLK), .clr(Reset));
  Register #(.width(11)) register_11 (
    .D(ByteAddress[15:5]), .en(demultiplexer_1_out4), .Q(register_11_q), .clk(CLK), .clr(Reset));
  assign {controlled_buffer_1_out_4, controlled_buffer_1_out_3, controlled_buffer_1_out_2, controlled_buffer_1_out} = demultiplexer_2_out4 ? register_12_q : 32'bz;  // Controlled_Buffer controlled_buffer_4
  Register #(.width(32)) register_12 (
    .D(BlockDataInput), .en(demultiplexer_1_out4), .Q(register_12_q), .clk(CLK), .clr(Reset));
  Register #(.width(1)) register_13 (
    .D(1'b1), .en(demultiplexer_1_out3), .Q(register_13_q[11]), .clk(CLK), .clr(Reset));
  Register #(.width(11)) register_14 (
    .D(ByteAddress[15:5]), .en(demultiplexer_1_out3), .Q(register_14_q), .clk(CLK), .clr(Reset));
  Register #(.width(32)) register_15 (
    .D(BlockDataInput), .en(demultiplexer_1_out3), .Q(register_15_q), .clk(CLK), .clr(Reset));
  assign {controlled_buffer_1_out_4, controlled_buffer_1_out_3, controlled_buffer_1_out_2, controlled_buffer_1_out} = demultiplexer_2_out3 ? register_15_q : 32'bz;  // Controlled_Buffer controlled_buffer_5
  Register #(.width(1)) register_16 (
    .D(1'b1), .en(demultiplexer_1_out2), .Q(register_16_q[11]), .clk(CLK), .clr(Reset));
  Register #(.width(11)) register_17 (
    .D(ByteAddress[15:5]), .en(demultiplexer_1_out2), .Q(register_17_q), .clk(CLK), .clr(Reset));
  Register #(.width(32)) register_18 (
    .D(BlockDataInput), .en(demultiplexer_1_out2), .Q(register_18_q), .clk(CLK), .clr(Reset));
  Register #(.width(1)) register_19 (
    .D(1'b1), .en(demultiplexer_1_out1), .Q(register_20_q[11]), .clk(CLK), .clr(Reset));
  Register #(.width(11)) register_20 (
    .D(ByteAddress[15:5]), .en(demultiplexer_1_out1), .Q(register_20_q[10:0]), .clk(CLK), .clr(Reset));
  Register #(.width(32)) register_21 (
    .D(BlockDataInput), .en(demultiplexer_1_out1), .Q(register_21_q), .clk(CLK), .clr(Reset));
  assign {controlled_buffer_1_out_4, controlled_buffer_1_out_3, controlled_buffer_1_out_2, controlled_buffer_1_out} = demultiplexer_2_out2 ? register_18_q : 32'bz;  // Controlled_Buffer controlled_buffer_6
  assign {controlled_buffer_1_out_4, controlled_buffer_1_out_3, controlled_buffer_1_out_2, controlled_buffer_1_out} = demultiplexer_2_out1 ? register_21_q : 32'bz;  // Controlled_Buffer controlled_buffer_7
  Register #(.width(1)) register_22 (
    .D(1'b1), .en(demultiplexer_1_out0), .Q(register_23_q[11]), .clk(CLK), .clr(Reset));
  Register #(.width(11)) register_23 (
    .D(ByteAddress[15:5]), .en(demultiplexer_1_out0), .Q(register_23_q[10:0]), .clk(CLK), .clr(Reset));
  assign {controlled_buffer_1_out_4, controlled_buffer_1_out_3, controlled_buffer_1_out_2, controlled_buffer_1_out} = demultiplexer_2_out0 ? register_24_q : 32'bz;  // Controlled_Buffer controlled_buffer_8
  Register #(.width(32)) register_24 (
    .D(BlockDataInput), .en(demultiplexer_1_out0), .Q(register_24_q), .clk(CLK), .clr(Reset));
  Multiplexer #(.select(2), .width(8)) multiplexer_1 (
    .in0(controlled_buffer_1_out), .in1(controlled_buffer_1_out_2), .in2(controlled_buffer_1_out_3),
    .in3(controlled_buffer_1_out_4), .out(DataOutput), .sel(ByteAddress[1:0]), .en(comparator_1_eq));
  Multiplexer #(.select(3), .width(12), .enable("false")) multiplexer_2 (
    .in0(register_23_q), .in1(register_20_q), .in2({register_16_q[11], register_17_q}),
    .in3({register_13_q[11], register_14_q}), .in4({register_10_q[11], register_11_q}), .in5(register_8_q),
    .in6(register_5_q), .in7(register_2_q), .out(multiplexer_2_out), .sel(ByteAddress[4:2]));
  not not_1 (Miss, comparator_1_eq);
  Comparator #(.width(12)) comparator_1 (
    .a(multiplexer_2_out), .b({1'b1, ByteAddress[15:5]}), .eq(comparator_1_eq));  // open: gt, lt
  Demultiplexer #(.select(3), .enable("false")) demultiplexer_2 (
    .out0(demultiplexer_2_out0), .out1(demultiplexer_2_out1), .out2(demultiplexer_2_out2),
    .out3(demultiplexer_2_out3), .out4(demultiplexer_2_out4), .out5(demultiplexer_2_out5),
    .out6(demultiplexer_2_out6), .out7(demultiplexer_2_out7), .in(comparator_1_eq), .sel(ByteAddress[4:2]));

  // Notes on the sheet:
  //   Input
  //   Output
endmodule
