// Logisim project Lab3 - CPU.circ as structural Verilog: 6 circuits, main circuit 32-bit SingleCycleCPU
module RegisterFile (
  input  [4:0] ReadRegister1_num,
  input  [31:0] WriteData,
  input  [4:0] ReadRegister2_num,
  input  [4:0] WriteRegister_num,
  input  Reset,
  input  RegisterWrite,
  input  CLK,
  output [31:0] ReadData1,
  output [31:0] ReadData2
);

  wire and_1_out, and_2_out, and_3_out, and_4_out, and_5_out, and_6_out, and_7_out, and_8_out, and_9_out,
       and_10_out, and_11_out, and_12_out, and_13_out, and_14_out, and_15_out, and_16_out, and_17_out,
       and_18_out, and_19_out, and_20_out, and_21_out, and_22_out, and_23_out, and_24_out, and_25_out,
       and_26_out, and_27_out, and_28_out, and_29_out, and_30_out, and_31_out, and_32_out, W0, W1, W2, W3,
       W4, W5, W6, W7, W8, W9, W10, W11, W12, W13, W14, W15, W16, W17, W18, W19, W20, W21, W22, W23, W24,
       W25, W26, W27, W28, W29, W30, W31;
  wire [31:0] R0, R1, R2, R3, R4, R5, R6, R7, R8, R9, R10, R11, R12, R13, R14, R15, R16, R17, R18, R19, R20,
       R21, R22, R23, R24, R25, R26, R27, R28, R29, R30, R31;

  Decoder #(.select(5), .enable("false")) decoder_1 (
    .out0(W0), .out1(W1), .out2(W2), .out3(W3), .out4(W4), .out5(W5), .out6(W6), .out7(W7), .out8(W8),
    .out9(W9), .out10(W10), .out11(W11), .out12(W12), .out13(W13), .out14(W14), .out15(W15), .out16(W16),
    .out17(W17), .out18(W18), .out19(W19), .out20(W20), .out21(W21), .out22(W22), .out23(W23), .out24(W24),
    .out25(W25), .out26(W26), .out27(W27), .out28(W28), .out29(W29), .out30(W30), .out31(W31),
    .sel(WriteRegister_num));
  and and_1 (and_1_out, RegisterWrite, W0);
  and and_2 (and_2_out, RegisterWrite, W8);
  and and_3 (and_3_out, RegisterWrite, W16);
  and and_4 (and_4_out, RegisterWrite, W24);
  Register #(.width(32)) register_1 (.D(WriteData), .en(and_1_out), .Q(R0), .clk(CLK), .clr(Reset));
  Register #(.width(32)) register_2 (.D(WriteData), .en(and_2_out), .Q(R8), .clk(CLK), .clr(Reset));
  Register #(.width(32)) register_3 (.D(WriteData), .en(and_3_out), .Q(R16), .clk(CLK), .clr(Reset));
  Register #(.width(32)) register_4 (.D(WriteData), .en(and_4_out), .Q(R24), .clk(CLK), .clr(Reset));
  Multiplexer #(.select(5), .width(32), .enable("false")) multiplexer_1 (
    .in0(R0), .in1(R1), .in2(R2), .in3(R3), .in4(R4), .in5(R5), .in6(R6), .in7(R7), .in8(R8), .in9(R9),
    .in10(R10), .in11(R11), .in12(R12), .in13(R13), .in14(R14), .in15(R15), .in16(R16), .in17(R17),
    .in18(R18), .in19(R19), .in20(R20), .in21(R21), .in22(R22), .in23(R23), .in24(R24), .in25(R25),
    .in26(R26), .in27(R27), .in28(R28), .in29(R29), .in30(R30), .in31(R31), .out(ReadData1),
    .sel(ReadRegister1_num));
  and and_5 (and_5_out, RegisterWrite, W1);
  and and_6 (and_6_out, RegisterWrite, W9);
  and and_7 (and_7_out, RegisterWrite, W17);
  and and_8 (and_8_out, RegisterWrite, W25);
  Register #(.width(32)) register_5 (.D(WriteData), .en(and_5_out), .Q(R1), .clk(CLK), .clr(Reset));
  Register #(.width(32)) register_6 (.D(WriteData), .en(and_6_out), .Q(R9), .clk(CLK), .clr(Reset));
  Register #(.width(32)) register_7 (.D(WriteData), .en(and_7_out), .Q(R17), .clk(CLK), .clr(Reset));
  Register #(.width(32)) register_8 (.D(WriteData), .en(and_8_out), .Q(R25), .clk(CLK), .clr(Reset));
  and and_9 (and_9_out, RegisterWrite, W2);
  and and_10 (and_10_out, RegisterWrite, W10);
  and and_11 (and_11_out, RegisterWrite, W18);
  and and_12 (and_12_out, RegisterWrite, W26);
  Register #(.width(32)) register_9 (.D(WriteData), .en(and_9_out), .Q(R2), .clk(CLK), .clr(Reset));
  Register #(.width(32)) register_10 (.D(WriteData), .en(and_10_out), .Q(R10), .clk(CLK), .clr(Reset));
  Register #(.width(32)) register_11 (.D(WriteData), .en(and_11_out), .Q(R18), .clk(CLK), .clr(Reset));
  Register #(.width(32)) register_12 (.D(WriteData), .en(and_12_out), .Q(R26), .clk(CLK), .clr(Reset));
  and and_13 (and_13_out, RegisterWrite, W3);
  and and_14 (and_14_out, RegisterWrite, W11);
  and and_15 (and_15_out, RegisterWrite, W19);
  and and_16 (and_16_out, RegisterWrite, W27);
  Register #(.width(32)) register_13 (.D(WriteData), .en(and_13_out), .Q(R3), .clk(CLK), .clr(Reset));
  Register #(.width(32)) register_14 (.D(WriteData), .en(and_14_out), .Q(R11), .clk(CLK), .clr(Reset));
  Register #(.width(32)) register_15 (.D(WriteData), .en(and_15_out), .Q(R19), .clk(CLK), .clr(Reset));
  Register #(.width(32)) register_16 (.D(WriteData), .en(and_16_out), .Q(R27), .clk(CLK), .clr(Reset));
  and and_17 (and_17_out, RegisterWrite, W4);
  and and_18 (and_18_out, RegisterWrite, W12);
  and and_19 (and_19_out, RegisterWrite, W20);
  and and_20 (and_20_out, RegisterWrite, W28);
  Register #(.width(32)) register_17 (.D(WriteData), .en(and_17_out), .Q(R4), .clk(CLK), .clr(Reset));
  Register #(.width(32)) register_18 (.D(WriteData), .en(and_18_out), .Q(R12), .clk(CLK), .clr(Reset));
  Register #(.width(32)) register_19 (.D(WriteData), .en(and_19_out), .Q(R20), .clk(CLK), .clr(Reset));
  Register #(.width(32)) register_20 (.D(WriteData), .en(and_20_out), .Q(R28), .clk(CLK), .clr(Reset));
  Multiplexer #(.select(5), .width(32), .enable("false")) multiplexer_2 (
    .in0(R0), .in1(R1), .in2(R2), .in3(R3), .in4(R4), .in5(R5), .in6(R6), .in7(R7), .in8(R8), .in9(R9),
    .in10(R10), .in11(R11), .in12(R12), .in13(R13), .in14(R14), .in15(R15), .in16(R16), .in17(R17),
    .in18(R18), .in19(R19), .in20(R20), .in21(R21), .in22(R22), .in23(R23), .in24(R24), .in25(R25),
    .in26(R26), .in27(R27), .in28(R28), .in29(R29), .in30(R30), .in31(R31), .out(ReadData2),
    .sel(ReadRegister2_num));
  and and_21 (and_21_out, RegisterWrite, W5);
  and and_22 (and_22_out, RegisterWrite, W13);
  and and_23 (and_23_out, RegisterWrite, W21);
  and and_24 (and_24_out, RegisterWrite, W29);
  Register #(.width(32)) register_21 (.D(WriteData), .en(and_21_out), .Q(R5), .clk(CLK), .clr(Reset));
  Register #(.width(32)) register_22 (.D(WriteData), .en(and_22_out), .Q(R13), .clk(CLK), .clr(Reset));
  Register #(.width(32)) register_23 (.D(WriteData), .en(and_23_out), .Q(R21), .clk(CLK), .clr(Reset));
  Register #(.width(32)) register_24 (.D(WriteData), .en(and_24_out), .Q(R29), .clk(CLK), .clr(Reset));
  and and_25 (and_25_out, RegisterWrite, W6);
  and and_26 (and_26_out, RegisterWrite, W14);
  and and_27 (and_27_out, RegisterWrite, W22);
  and and_28 (and_28_out, RegisterWrite, W30);
  Register #(.width(32)) register_25 (.D(WriteData), .en(and_25_out), .Q(R6), .clk(CLK), .clr(Reset));
  Register #(.width(32)) register_26 (.D(WriteData), .en(and_26_out), .Q(R14), .clk(CLK), .clr(Reset));
  Register #(.width(32)) register_27 (.D(WriteData), .en(and_27_out), .Q(R22), .clk(CLK), .clr(Reset));
  Register #(.width(32)) register_28 (.D(WriteData), .en(and_28_out), .Q(R30), .clk(CLK), .clr(Reset));
  and and_29 (and_29_out, RegisterWrite, W7);
  and and_30 (and_30_out, RegisterWrite, W15);
  and and_31 (and_31_out, RegisterWrite, W23);
  and and_32 (and_32_out, RegisterWrite, W31);
  Register #(.width(32)) register_29 (.D(WriteData), .en(and_29_out), .Q(R7), .clk(CLK), .clr(Reset));
  Register #(.width(32)) register_30 (.D(WriteData), .en(and_30_out), .Q(R15), .clk(CLK), .clr(Reset));
  Register #(.width(32)) register_31 (.D(WriteData), .en(and_31_out), .Q(R23), .clk(CLK), .clr(Reset));
  Register #(.width(32)) register_32 (.D(WriteData), .en(and_32_out), .Q(R31), .clk(CLK), .clr(Reset));

  // Notes on the sheet:
  //   Input
  //   Output
endmodule

module Sign_extend (
  input  [31:0] Instruction_31_0,
  output [31:0] Extended_data
);

  wire [31:0] bit_extender_1_out, bit_extender_2_out;

  assign bit_extender_1_out = {{23{Instruction_31_0[20]}}, Instruction_31_0[20:12]};  // Bit_Extender bit_extender_1
  assign bit_extender_2_out = {{13{Instruction_31_0[23]}}, Instruction_31_0[23:5]};  // Bit_Extender bit_extender_2
  Multiplexer #(.width(32), .enable("false")) multiplexer_1 (
    .in0(bit_extender_1_out), .in1(bit_extender_2_out), .out(Extended_data), .sel(Instruction_31_0[26]));

  // Notes on the sheet:
  //   Input
  //   Output
endmodule

module ALUControl (
  input  ALUOp1,
  input  I_30,
  input  ALUOp0,
  input  I_29,
  input  I_24,
  output ALUControl_0,
  output ALUControl_2,
  output ALUControl_1,
  output ALUControl_3
);

  wire and_1_out, and_2_out, and_3_out, and_4_out, and_5_out, and_6_out, and_7_out, not_1_out, not_2_out,
       not_3_out;

  not not_1 (not_1_out, I_24);
  not not_2 (not_2_out, ALUOp1);
  not not_3 (not_3_out, I_24);
  and and_1 (and_1_out, ALUOp1, I_29, I_24);
  and and_2 (and_2_out, ALUOp1, I_30, not_1_out);
  or or_1 (ALUControl_3, and_1_out, and_2_out, and_3_out);
  and and_3 (and_3_out, ALUOp1, ALUOp0);
  and and_4 (and_4_out, ALUOp1, I_29, I_24);
  or or_2 (ALUControl_2, ALUOp0, and_4_out, and_5_out);
  and and_5 (and_5_out, ALUOp1, I_30);
  or or_3 (ALUControl_1, not_2_out, I_24, I_30, ALUOp0);
  and and_6 (and_6_out, ALUOp1, I_29);
  or or_4 (ALUControl_0, ALUOp0, and_6_out, and_7_out);
  and and_7 (and_7_out, ALUOp1, I_30, not_3_out);

  // Notes on the sheet:
  //   Input
  //   Output
endmodule

module ControlUnit (
  input  [10:0] Instruction_31_21,
  output Reg2Loc,
  output Branch,
  output ALUSrc,
  output ALUOp1,
  output MemtoReg,
  output ALUOp0,
  output RegWrite,
  output MemRead,
  output MemWrite
);

  wire not_1_out, not_2_out, not_3_out, not_4_out, not_5_out, not_6_out, not_7_out, not_8_out, not_9_out,
       not_10_out, not_11_out, not_12_out, not_13_out, not_14_out, not_15_out, not_16_out, not_17_out,
       not_18_out, not_19_out, not_20_out;

  not not_1 (not_1_out, Instruction_31_21[9]);
  not not_2 (not_2_out, Instruction_31_21[6]);
  not not_3 (not_3_out, Instruction_31_21[4]);
  not not_4 (not_4_out, Instruction_31_21[3]);
  not not_5 (not_5_out, Instruction_31_21[5]);
  not not_6 (not_6_out, Instruction_31_21[4]);
  not not_7 (not_7_out, Instruction_31_21[3]);
  not not_8 (not_8_out, Instruction_31_21[2]);
  not not_9 (not_9_out, Instruction_31_21[1]);
  not not_10 (not_10_out, Instruction_31_21[0]);
  not not_11 (not_11_out, Instruction_31_21[5]);
  not not_12 (not_12_out, Instruction_31_21[4]);
  not not_13 (not_13_out, Instruction_31_21[3]);
  not not_14 (not_14_out, Instruction_31_21[2]);
  not not_15 (not_15_out, Instruction_31_21[0]);
  not not_16 (not_16_out, Instruction_31_21[7]);
  not not_17 (not_17_out, Instruction_31_21[5]);
  not not_18 (not_18_out, Instruction_31_21[2]);
  not not_19 (not_19_out, Instruction_31_21[1]);
  not not_20 (not_20_out, Instruction_31_21[0]);
  and and_1 (ALUOp0, Instruction_31_21[10], not_1_out, Instruction_31_21[8], Instruction_31_21[7], not_2_out, Instruction_31_21[5], not_3_out, not_4_out);
  and and_2 (MemWrite, Instruction_31_21[10], Instruction_31_21[9], Instruction_31_21[8], Instruction_31_21[7], Instruction_31_21[6], not_5_out, not_6_out, not_7_out, not_8_out, not_9_out, not_10_out);
  and and_3 (MemRead, Instruction_31_21[10], Instruction_31_21[9], Instruction_31_21[8], Instruction_31_21[7], Instruction_31_21[6], not_11_out, not_12_out, not_13_out, not_14_out, Instruction_31_21[1], not_15_out);
  and and_4 (ALUOp1, Instruction_31_21[10], not_16_out, Instruction_31_21[6], not_17_out, Instruction_31_21[4], not_18_out, not_19_out, not_20_out);
  or or_1 (Reg2Loc, ALUOp0, MemWrite);
  or or_2 (ALUSrc, MemWrite, MemRead);
  or or_3 (RegWrite, MemRead, ALUOp1);

  assign Branch = ALUOp0;
  assign MemtoReg = MemRead;

  // Notes on the sheet:
  //   Input
  //   Output
endmodule

module _32_bit_SingleCycleCPU (
);

  wire ALUOp0, ALUOp1, ALUSrc, and_1_out, Branch, CLK, MemRead, MemtoReg, MemWrite, n32_bit_alu_3_zero,
       Reg2Loc, RegWrite, Reset;
  wire [3:0] ALUControl;
  wire [4:0] multiplexer_1_out;
  wire [10:0] Instruction_31_21;
  wire [11:0] n32_bit_alu_3_result_2;
  wire [15:0] PC_q_2;
  wire [20:0] rom_1_data;
  wire [31:0] multiplexer_2_out, multiplexer_3_out, multiplexer_4_out, n32_bit_alu_1_result,
       n32_bit_alu_2_result, n32_bit_alu_3_result, PC_q, ram_1_data, registerfile_1_readdata1,
       registerfile_1_readdata2, shifter_1_out, sign_extend_1_extended_data;

  Button u_Reset (.out(Reset));
  Register #(.width(32)) PC (
    .D(multiplexer_3_out), .Q({PC_q[31:18], PC_q_2, PC_q[1:0]}), .clk(CLK), .clr(Reset));  // open: en
  Clock clock_1 (.out(CLK));
  ControlUnit controlunit_1 (
    .Reg2Loc(Reg2Loc), .Branch(Branch), .Instruction_31_21(Instruction_31_21), .ALUSrc(ALUSrc),
    .ALUOp1(ALUOp1), .MemtoReg(MemtoReg), .ALUOp0(ALUOp0), .RegWrite(RegWrite), .MemRead(MemRead),
    .MemWrite(MemWrite));
  _32_bit_ALU u_32_bit_alu_1 (
    .ALUOp(4'b0010), .a({PC_q[31:18], PC_q_2, PC_q[1:0]}), .b(32'h4), .Result(n32_bit_alu_1_result));  // open: Overflow, Zero
  ROM #(.addrWidth(16), .dataWidth(32)) rom_1 (.addr(PC_q_2), .data({Instruction_31_21, rom_1_data}), .sel(1'b1));
  Multiplexer #(.width(5), .enable("false")) multiplexer_1 (
    .in0(rom_1_data[20:16]), .in1(rom_1_data[4:0]), .out(multiplexer_1_out), .sel(Reg2Loc));
  RegisterFile registerfile_1 (
    .ReadRegister1_num(rom_1_data[9:5]), .WriteData(multiplexer_4_out), .ReadData1(registerfile_1_readdata1),
    .ReadData2(registerfile_1_readdata2), .ReadRegister2_num(multiplexer_1_out),
    .WriteRegister_num(rom_1_data[4:0]), .Reset(Reset), .RegisterWrite(RegWrite), .CLK(CLK));
  Sign_extend sign_extend_1 (
    .Instruction_31_0({Instruction_31_21, rom_1_data}), .Extended_data(sign_extend_1_extended_data));
  ALUControl alucontrol_1 (
    .ALUOp1(ALUOp1), .ALUOp0(ALUOp0), .ALUControl_3(ALUControl[3]), .I_30(Instruction_31_21[9]),
    .ALUControl_2(ALUControl[2]), .I_29(Instruction_31_21[8]), .ALUControl_1(ALUControl[1]),
    .I_24(Instruction_31_21[3]), .ALUControl_0(ALUControl[0]));
  Shifter #(.width(32)) shifter_1 (.in(sign_extend_1_extended_data), .\dist (5'b00010), .out(shifter_1_out));
  Multiplexer #(.width(32), .enable("false")) multiplexer_2 (
    .in0(registerfile_1_readdata2), .in1(sign_extend_1_extended_data), .out(multiplexer_2_out), .sel(ALUSrc));
  _32_bit_ALU u_32_bit_alu_2 (
    .ALUOp(4'b0010), .a({PC_q[31:18], PC_q_2, PC_q[1:0]}), .b(shifter_1_out), .Result(n32_bit_alu_2_result));  // open: Overflow, Zero
  _32_bit_ALU u_32_bit_alu_3 (
    .ALUOp(ALUControl), .a(registerfile_1_readdata1), .b(multiplexer_2_out),
    .Result({n32_bit_alu_3_result[31:14], n32_bit_alu_3_result_2, n32_bit_alu_3_result[1:0]}),
    .Zero(n32_bit_alu_3_zero));  // open: Overflow
  and and_1 (and_1_out, Branch, n32_bit_alu_3_zero);
  // Probe on multiplexer_3_out
  Multiplexer #(.width(32), .enable("false")) multiplexer_3 (
    .in0(n32_bit_alu_1_result), .in1(n32_bit_alu_2_result), .out(multiplexer_3_out), .sel(and_1_out));
  RAM #(.addrWidth(12), .dataWidth(32), .bus("separate")) ram_1 (
    .addr(n32_bit_alu_3_result_2), .din(registerfile_1_readdata2), .data(ram_1_data), .str(MemWrite),
    .sel(1'b1), .clk(CLK), .ld(MemRead));  // open: clr
  Multiplexer #(.width(32), .enable("false")) multiplexer_4 (
    .in0({n32_bit_alu_3_result[31:14], n32_bit_alu_3_result_2, n32_bit_alu_3_result[1:0]}), .in1(ram_1_data),
    .out(multiplexer_4_out), .sel(MemtoReg));
  // Probe on multiplexer_4_out

  // Notes on the sheet:
  //   Do not change the value in ROM
  //   contents of rom_1 (hex, n*v repeats v):
  //   f841804d f845006e 8b0e01a9 8a0901aa aa0a012b cb09016c f802004c b4ffff33
  //   You don't have to connect the RAM "reset", otherwise, you will have to input initial values after each reset.
  //   The 32-bit ALU designed in Lab2 is needed for the CPU design. Before using the ALU in the CPU design, change the “set on less than” function to “pass b”. 
endmodule

module extral (
  input  ALUOp1,
  input  ALUOp0,
  input  I30,
  input  I29,
  input  I24,
  output ALUControl3,
  output ALUControl2,
  output ALUControl1,
  output ALUControl0
);

  wire and_1_out, and_2_out, and_3_out, and_4_out, and_5_out, and_6_out, and_7_out, not_1_out, not_2_out,
       not_3_out;

  not not_1 (not_1_out, I24);
  and and_1 (and_1_out, ALUOp1, I29, I24);
  and and_2 (and_2_out, ALUOp1, I30);
  not not_2 (not_2_out, ALUOp1);
  not not_3 (not_3_out, I24);
  and and_3 (and_3_out, ALUOp1, I29, I24);
  and and_4 (and_4_out, ALUOp1, I30, not_1_out);
  and and_5 (and_5_out, ALUOp1, ALUOp0);
  or or_1 (ALUControl2, ALUOp0, and_1_out, and_2_out);
  or or_2 (ALUControl1, not_2_out, I24, I30, ALUOp0);
  and and_6 (and_6_out, ALUOp1, I29);
  and and_7 (and_7_out, ALUOp1, I30, not_3_out);
  or or_3 (ALUControl3, and_3_out, and_4_out, and_5_out);
  or or_4 (ALUControl0, ALUOp0, and_6_out, and_7_out);
endmodule
