// Logisim project Lab1 - Stopwatch.circ as structural Verilog: 17 circuits, main circuit 2-channel 1-bit multiplexer
module _2_channel_1_bit_multiplexer (
  input  Input0,
  input  Input1,
  input  Sel,
  output Output
);

  wire and_1_out, and_2_out, not_1_out;

  not not_1 (not_1_out, Sel);
  and and_1 (and_1_out, not_1_out, Input0);
  and and_2 (and_2_out, Sel, Input1);
  or or_1 (Output, and_1_out, and_2_out);

  // Notes on the sheet:
  //   Function: 
  //   Input
  //   If Sel==0, then Output =Input0; If Sel==1, then Output=Input1;
  //   Output
endmodule

module _2_channel_16_bit_multiplexer (
  input  [15:0] Input0,
  input  [15:0] Input1,
  input  Sel,
  output [15:0] Output
);

  _2_channel_1_bit_multiplexer u_2_channel_1_bit_multiplexer_1 (
    .Input0(Input0[0]), .Input1(Input1[0]), .Output(Output[0]), .Sel(Sel));
  _2_channel_1_bit_multiplexer u_2_channel_1_bit_multiplexer_2 (
    .Input0(Input0[1]), .Input1(Input1[1]), .Output(Output[1]), .Sel(Sel));
  _2_channel_1_bit_multiplexer u_2_channel_1_bit_multiplexer_3 (
    .Input0(Input0[2]), .Input1(Input1[2]), .Output(Output[2]), .Sel(Sel));
  _2_channel_1_bit_multiplexer u_2_channel_1_bit_multiplexer_4 (
    .Input0(Input0[3]), .Input1(Input1[3]), .Output(Output[3]), .Sel(Sel));
  _2_channel_1_bit_multiplexer u_2_channel_1_bit_multiplexer_5 (
    .Input0(Input0[4]), .Input1(Input1[4]), .Output(Output[4]), .Sel(Sel));
  _2_channel_1_bit_multiplexer u_2_channel_1_bit_multiplexer_6 (
    .Input0(Input0[5]), .Input1(Input1[5]), .Output(Output[5]), .Sel(Sel));
  _2_channel_1_bit_multiplexer u_2_channel_1_bit_multiplexer_7 (
    .Input0(Input0[6]), .Input1(Input1[6]), .Output(Output[6]), .Sel(Sel));
  _2_channel_1_bit_multiplexer u_2_channel_1_bit_multiplexer_8 (
    .Input0(Input0[7]), .Input1(Input1[7]), .Output(Output[7]), .Sel(Sel));
  _2_channel_1_bit_multiplexer u_2_channel_1_bit_multiplexer_9 (
    .Input0(Input0[8]), .Input1(Input1[8]), .Output(Output[8]), .Sel(Sel));
  _2_channel_1_bit_multiplexer u_2_channel_1_bit_multiplexer_10 (
    .Input0(Input0[9]), .Input1(Input1[9]), .Output(Output[9]), .Sel(Sel));
  _2_channel_1_bit_multiplexer u_2_channel_1_bit_multiplexer_11 (
    .Input0(Input0[10]), .Input1(Input1[10]), .Output(Output[10]), .Sel(Sel));
  _2_channel_1_bit_multiplexer u_2_channel_1_bit_multiplexer_12 (
    .Input0(Input0[11]), .Input1(Input1[11]), .Output(Output[11]), .Sel(Sel));
  _2_channel_1_bit_multiplexer u_2_channel_1_bit_multiplexer_13 (
    .Input0(Input0[12]), .Input1(Input1[12]), .Output(Output[12]), .Sel(Sel));
  _2_channel_1_bit_multiplexer u_2_channel_1_bit_multiplexer_14 (
    .Input0(Input0[13]), .Input1(Input1[13]), .Output(Output[13]), .Sel(Sel));
  _2_channel_1_bit_multiplexer u_2_channel_1_bit_multiplexer_15 (
    .Input0(Input0[14]), .Input1(Input1[14]), .Output(Output[14]), .Sel(Sel));
  _2_channel_1_bit_multiplexer u_2_channel_1_bit_multiplexer_16 (
    .Input0(Input0[15]), .Input1(Input1[15]), .Output(Output[15]), .Sel(Sel));

  // Notes on the sheet:
  //   Function: 
  //   Input
  //   If Sel==0, then Output =Input0; If Sel==1, then Output=Input1;
  //   Output
endmodule

module _1_bit_unsigned_comparator (
  input  a0,
  input  b0,
  output Greater,
  output Equal,
  output Less
);

  wire not_1_out, not_2_out;

  not not_1 (not_1_out, b0);
  not not_2 (not_2_out, a0);
  and and_1 (Greater, a0, not_1_out);
  and and_2 (Less, not_2_out, b0);
  nor nor_1 (Equal, Greater, Less);

  // Notes on the sheet:
  //   Function: 
  //   Input
  //   If a0 == b0, then only Equal =1; If a0<b0, then only Less = 1; If a0>b0, then only Greater = 1;
  //   Output
endmodule

module _4_bit_unsigned_comparator (
  input  [3:0] a,
  input  [3:0] b,
  output Greater,
  output Equal,
  output Less
);

  wire and_1_out, and_2_out, and_3_out, and_4_out, and_5_out, and_6_out, n1_bit_unsigned_comparator_1_equal,
       n1_bit_unsigned_comparator_1_greater, n1_bit_unsigned_comparator_1_less,
       n1_bit_unsigned_comparator_2_equal, n1_bit_unsigned_comparator_2_greater,
       n1_bit_unsigned_comparator_2_less, n1_bit_unsigned_comparator_3_equal,
       n1_bit_unsigned_comparator_3_greater, n1_bit_unsigned_comparator_3_less,
       n1_bit_unsigned_comparator_4_equal, n1_bit_unsigned_comparator_4_greater,
       n1_bit_unsigned_comparator_4_less;

  _1_bit_unsigned_comparator u_1_bit_unsigned_comparator_1 (
    .Greater(n1_bit_unsigned_comparator_1_greater), .a0(a[3]), .Equal(n1_bit_unsigned_comparator_1_equal),
    .b0(b[3]), .Less(n1_bit_unsigned_comparator_1_less));
  _1_bit_unsigned_comparator u_1_bit_unsigned_comparator_2 (
    .Greater(n1_bit_unsigned_comparator_2_greater), .a0(a[2]), .Equal(n1_bit_unsigned_comparator_2_equal),
    .b0(b[2]), .Less(n1_bit_unsigned_comparator_2_less));
  _1_bit_unsigned_comparator u_1_bit_unsigned_comparator_3 (
    .Greater(n1_bit_unsigned_comparator_3_greater), .a0(a[1]), .Equal(n1_bit_unsigned_comparator_3_equal),
    .b0(b[1]), .Less(n1_bit_unsigned_comparator_3_less));
  _1_bit_unsigned_comparator u_1_bit_unsigned_comparator_4 (
    .Greater(n1_bit_unsigned_comparator_4_greater), .a0(a[0]), .Equal(n1_bit_unsigned_comparator_4_equal),
    .b0(b[0]), .Less(n1_bit_unsigned_comparator_4_less));
  and and_1 (and_1_out, n1_bit_unsigned_comparator_1_equal, n1_bit_unsigned_comparator_2_greater);
  and and_2 (and_2_out, n1_bit_unsigned_comparator_1_equal, n1_bit_unsigned_comparator_2_less);
  and and_3 (and_3_out, n1_bit_unsigned_comparator_1_equal, n1_bit_unsigned_comparator_2_equal, n1_bit_unsigned_comparator_3_greater);
  and and_4 (and_4_out, n1_bit_unsigned_comparator_1_equal, n1_bit_unsigned_comparator_2_equal, n1_bit_unsigned_comparator_3_less);
  and and_5 (and_5_out, n1_bit_unsigned_comparator_1_equal, n1_bit_unsigned_comparator_2_equal, n1_bit_unsigned_comparator_3_equal, n1_bit_unsigned_comparator_4_greater);
  and and_6 (and_6_out, n1_bit_unsigned_comparator_1_equal, n1_bit_unsigned_comparator_2_equal, n1_bit_unsigned_comparator_3_equal, n1_bit_unsigned_comparator_4_less);
  and and_7 (Equal, n1_bit_unsigned_comparator_1_equal, n1_bit_unsigned_comparator_2_equal, n1_bit_unsigned_comparator_3_equal, n1_bit_unsigned_comparator_4_equal);
  or or_1 (Greater, n1_bit_unsigned_comparator_1_greater, and_1_out, and_3_out, and_5_out);
  or or_2 (Less, n1_bit_unsigned_comparator_1_less, and_2_out, and_4_out, and_6_out);

  // Notes on the sheet:
  //   Function: 
  //   Input
  //   If a == b, then only Equal =1; If a<b, then only Less = 1; If a>b, then only Greater = 1;
  //   Output
endmodule

module _16_bit_unsigned_comparator (
  input  [15:0] a,
  input  [15:0] b,
  output Greater,
  output Equal,
  output Less
);

  wire and_1_out, and_2_out, and_3_out, and_4_out, and_5_out, and_6_out, n4_bit_unsigned_comparator_1_equal,
       n4_bit_unsigned_comparator_1_greater, n4_bit_unsigned_comparator_1_less,
       n4_bit_unsigned_comparator_2_equal, n4_bit_unsigned_comparator_2_greater,
       n4_bit_unsigned_comparator_2_less, n4_bit_unsigned_comparator_3_equal,
       n4_bit_unsigned_comparator_3_greater, n4_bit_unsigned_comparator_3_less,
       n4_bit_unsigned_comparator_4_equal, n4_bit_unsigned_comparator_4_greater,
       n4_bit_unsigned_comparator_4_less;

  _4_bit_unsigned_comparator u_4_bit_unsigned_comparator_1 (
    .a(a[15:12]), .b(b[15:12]), .Greater(n4_bit_unsigned_comparator_1_greater),
    .Equal(n4_bit_unsigned_comparator_1_equal), .Less(n4_bit_unsigned_comparator_1_less));
  _4_bit_unsigned_comparator u_4_bit_unsigned_comparator_2 (
    .a(a[11:8]), .b(b[11:8]), .Greater(n4_bit_unsigned_comparator_2_greater),
    .Equal(n4_bit_unsigned_comparator_2_equal), .Less(n4_bit_unsigned_comparator_2_less));
  _4_bit_unsigned_comparator u_4_bit_unsigned_comparator_3 (
    .a(a[7:4]), .b(b[7:4]), .Greater(n4_bit_unsigned_comparator_3_greater),
    .Equal(n4_bit_unsigned_comparator_3_equal), .Less(n4_bit_unsigned_comparator_3_less));
  _4_bit_unsigned_comparator u_4_bit_unsigned_comparator_4 (
    .a(a[3:0]), .b(b[3:0]), .Greater(n4_bit_unsigned_comparator_4_greater),
    .Equal(n4_bit_unsigned_comparator_4_equal), .Less(n4_bit_unsigned_comparator_4_less));
  and and_1 (and_1_out, n4_bit_unsigned_comparator_1_equal, n4_bit_unsigned_comparator_2_greater);
  and and_2 (and_2_out, n4_bit_unsigned_comparator_1_equal, n4_bit_unsigned_comparator_2_less);
  and and_3 (and_3_out, n4_bit_unsigned_comparator_1_equal, n4_bit_unsigned_comparator_2_equal, n4_bit_unsigned_comparator_3_greater);
  and and_4 (and_4_out, n4_bit_unsigned_comparator_1_equal, n4_bit_unsigned_comparator_2_equal, n4_bit_unsigned_comparator_3_less);
  and and_5 (and_5_out, n4_bit_unsigned_comparator_1_equal, n4_bit_unsigned_comparator_2_equal, n4_bit_unsigned_comparator_3_equal, n4_bit_unsigned_comparator_4_greater);
  and and_6 (and_6_out, n4_bit_unsigned_comparator_1_equal, n4_bit_unsigned_comparator_2_equal, n4_bit_unsigned_comparator_3_equal, n4_bit_unsigned_comparator_4_less);
  and and_7 (Equal, n4_bit_unsigned_comparator_1_equal, n4_bit_unsigned_comparator_2_equal, n4_bit_unsigned_comparator_3_equal, n4_bit_unsigned_comparator_4_equal);
  or or_1 (Greater, n4_bit_unsigned_comparator_1_greater, and_1_out, and_3_out, and_5_out);
  or or_2 (Less, n4_bit_unsigned_comparator_1_less, and_2_out, and_4_out, and_6_out);

  // Notes on the sheet:
  //   Function: 
  //   Input
  //   If a == b, then only Equal =1; If a<b, then only Less = 1; If a>b, then only Greater = 1;
  //   Output
endmodule

module _7_Segment_Display_Control (
  input  Input0,
  input  Input1,
  input  Input2,
  input  Input3,
  output Output0,
  output Output4,
  output Output1,
  output Output5,
  output Output2,
  output Output6,
  output Output3
);

  wire and_1_out, and_2_out, and_3_out, and_4_out, and_5_out, and_6_out, and_7_out, and_8_out, and_9_out,
       and_10_out, and_11_out, and_12_out, and_13_out, and_14_out, and_15_out, and_16_out, and_17_out,
       and_18_out, and_19_out, and_20_out, and_21_out, and_22_out, and_23_out, and_24_out, and_25_out,
       and_26_out, and_27_out, and_28_out, and_29_out, and_30_out, and_31_out, and_32_out, and_33_out,
       and_34_out, and_35_out, not_1_out, not_2_out, not_3_out, not_4_out, not_5_out, not_6_out, not_7_out,
       not_8_out, not_9_out, not_10_out, not_11_out, not_12_out, not_13_out, not_14_out, not_15_out,
       not_16_out, not_17_out, not_18_out, not_19_out, not_20_out, not_21_out, not_22_out, not_23_out,
       not_24_out, not_25_out, not_26_out, not_27_out, not_28_out, not_29_out, not_30_out, not_31_out,
       not_32_out, not_33_out, not_34_out, not_35_out, not_36_out, not_37_out, not_38_out, not_39_out,
       not_40_out, not_41_out, not_42_out, not_43_out;

  not not_1 (not_1_out, Input2);
  not not_2 (not_2_out, Input0);
  not not_3 (not_3_out, Input3);
  not not_4 (not_4_out, Input1);
  not not_5 (not_5_out, Input2);
  not not_6 (not_6_out, Input1);
  not not_7 (not_7_out, Input0);
  not not_8 (not_8_out, Input3);
  not not_9 (not_9_out, Input1);
  not not_10 (not_10_out, Input0);
  not not_11 (not_11_out, Input2);
  not not_12 (not_12_out, Input2);
  not not_13 (not_13_out, Input0);
  not not_14 (not_14_out, Input3);
  not not_15 (not_15_out, Input3);
  not not_16 (not_16_out, Input2);
  not not_17 (not_17_out, Input1);
  not not_18 (not_18_out, Input0);
  not not_19 (not_19_out, Input3);
  not not_20 (not_20_out, Input2);
  not not_21 (not_21_out, Input3);
  not not_22 (not_22_out, Input1);
  not not_23 (not_23_out, Input0);
  not not_24 (not_24_out, Input2);
  not not_25 (not_25_out, Input0);
  not not_26 (not_26_out, Input3);
  not not_27 (not_27_out, Input1);
  not not_28 (not_28_out, Input3);
  not not_29 (not_29_out, Input1);
  not not_30 (not_30_out, Input3);
  not not_31 (not_31_out, Input1);
  not not_32 (not_32_out, Input3);
  not not_33 (not_33_out, Input2);
  not not_34 (not_34_out, Input3);
  not not_35 (not_35_out, Input2);
  not not_36 (not_36_out, Input0);
  not not_37 (not_37_out, Input2);
  not not_38 (not_38_out, Input1);
  not not_39 (not_39_out, Input0);
  not not_40 (not_40_out, Input1);
  not not_41 (not_41_out, Input2);
  not not_42 (not_42_out, Input0);
  not not_43 (not_43_out, Input0);
  and and_1 (and_1_out, not_1_out, Input1);
  and and_2 (and_2_out, Input1, not_2_out);
  and and_3 (and_3_out, not_3_out, Input2, not_4_out);
  and and_4 (and_4_out, Input3, not_5_out);
  and and_5 (and_5_out, Input3, Input0);
  and and_6 (and_6_out, not_6_out, not_7_out);
  and and_7 (and_7_out, not_8_out, Input2, not_9_out);
  and and_8 (and_8_out, Input2, not_10_out);
  and and_9 (and_9_out, Input3, not_11_out);
  and and_10 (and_10_out, Input3, Input1);
  and and_11 (and_11_out, not_12_out, not_13_out);
  and and_12 (and_12_out, not_14_out, Input1);
  and and_13 (and_13_out, not_15_out, Input2, Input0);
  and and_14 (and_14_out, Input2, Input1);
  and and_15 (and_15_out, Input3, not_16_out, not_17_out);
  and and_16 (and_16_out, Input3, not_18_out);
  and and_17 (and_17_out, not_19_out, not_20_out);
  and and_18 (and_18_out, not_21_out, not_22_out, not_23_out);
  and and_19 (and_19_out, not_24_out, not_25_out);
  and and_20 (and_20_out, not_26_out, Input1, Input0);
  and and_21 (and_21_out, Input3, not_27_out, Input0);
  and and_22 (and_22_out, not_28_out, not_29_out);
  and and_23 (and_23_out, not_30_out, Input0);
  and and_24 (and_24_out, not_31_out, Input0);
  and and_25 (and_25_out, not_32_out, Input2);
  and and_26 (and_26_out, Input3, not_33_out);
  and and_27 (and_27_out, not_34_out, not_35_out, not_36_out);
  and and_28 (and_28_out, not_37_out, Input1, Input0);
  and and_29 (and_29_out, Input2, not_38_out, Input0);
  and and_30 (and_30_out, Input2, Input1, not_39_out);
  and and_31 (and_31_out, Input3, not_40_out);
  and and_32 (and_32_out, not_41_out, not_42_out);
  and and_33 (and_33_out, Input1, not_43_out);
  and and_34 (and_34_out, Input3, Input1);
  and and_35 (and_35_out, Input3, Input2);
  or or_1 (Output0, and_1_out, and_2_out, and_3_out, and_4_out, and_5_out);
  or or_2 (Output1, and_6_out, and_7_out, and_8_out, and_9_out, and_10_out);
  or or_3 (Output2, and_11_out, and_12_out, and_13_out, and_14_out, and_15_out, and_16_out);
  or or_4 (Output3, and_17_out, and_18_out, and_19_out, and_20_out, and_21_out);
  or or_5 (Output4, and_22_out, and_23_out, and_24_out, and_25_out, and_26_out);
  or or_6 (Output5, and_27_out, and_28_out, and_29_out, and_30_out, and_31_out);
  or or_7 (Output6, and_32_out, and_33_out, and_34_out, and_35_out);
  _7_Segment_Display u_7_segment_display_1 (
    .g(Output0), .f(Output1), .a(Output2), .b(Output3), .e(Output6), .d(Output5), .c(Output4), .dp(1'b1));

  // Notes on the sheet:
  //   Function: 
  //   Input
  //   Output0 to Output6 control segment0 to segment6, respectively.
  //   Control a 7-segment display to show the hexadesimal data indicated by Input3 to Input0.
  //   Input3 is the Most Significant Bit (MSB), Input0 is the Least Significant Bit (LSB)
  //   For example, when Output3 is "1", the segment 3 wil be turned on.
  //   Output
  //   2
  //   1
  //   0
  //   6
  //   5
  //   3
  //   4
  //   Testing Circuit
endmodule

module _4_bit_Parallel_load_register (
  input  [3:0] Input,
  input  Reset,
  input  Enable,
  input  CLK,
  output [3:0] Output
);

  D_Flip_Flop d_ff_1 (.clk(CLK), .D(Input[3]), .Q(Output[3]), .en(Enable), .reset(Reset));  // open: Qn, preset
  D_Flip_Flop d_ff_2 (.clk(CLK), .D(Input[2]), .Q(Output[2]), .en(Enable), .reset(Reset));  // open: Qn, preset
  D_Flip_Flop d_ff_3 (.clk(CLK), .D(Input[1]), .Q(Output[1]), .en(Enable), .reset(Reset));  // open: Qn, preset
  D_Flip_Flop d_ff_4 (.clk(CLK), .D(Input[0]), .Q(Output[0]), .en(Enable), .reset(Reset));  // open: Qn, preset

  // Notes on the sheet:
  //   Function: 
  //   Input
  //   If "Reset" is 1, the register is reset to 0 asynchronously
  //   If "Enable" is 0, the CLK triggers will be ineffective
  //   At the CLK rising edge, Input is paralled loaded into the register
  //   Output
endmodule

module _16_bit_Parallel_load_register (
  input  [15:0] Input,
  input  Reset,
  input  Enable,
  input  CLK,
  output [15:0] Output
);

  _4_bit_Parallel_load_register u_4_bit_parallel_load_register_1 (
    .Input(Input[15:12]), .Reset(Reset), .Enable(Enable), .Output(Output[15:12]), .CLK(CLK));
  _4_bit_Parallel_load_register u_4_bit_parallel_load_register_2 (
    .Input(Input[11:8]), .Reset(Reset), .Enable(Enable), .Output(Output[11:8]), .CLK(CLK));
  _4_bit_Parallel_load_register u_4_bit_parallel_load_register_3 (
    .Input(Input[7:4]), .Reset(Reset), .Enable(Enable), .Output(Output[7:4]), .CLK(CLK));
  _4_bit_Parallel_load_register u_4_bit_parallel_load_register_4 (
    .Input(Input[3:0]), .Reset(Reset), .Enable(Enable), .Output(Output[3:0]), .CLK(CLK));

  // Notes on the sheet:
  //   Function: 
  //   Input
  //   If "Reset" is 1, the register is reset to 0 asynchronously
  //   If "Enable" is 0, the CLK triggers will be ineffective
  //   At the CLK rising edge, Input is paralled loaded into the register
  //   Output
endmodule

module _4_bit_BCD_Counter_State_Transition_Circuit (
  input  S3,
  input  S2,
  input  S1,
  input  S0,
  output N3,
  output N2,
  output N1,
  output N0
);

  wire and_1_out, and_2_out, and_3_out, and_4_out, and_5_out, and_6_out, and_7_out, and_8_out, and_9_out,
       not_1_out, not_2_out, not_3_out, not_4_out, not_5_out, not_6_out, not_7_out;

  not not_1 (not_1_out, S0);
  not not_2 (not_2_out, S2);
  not not_3 (not_3_out, S1);
  not not_4 (not_4_out, S0);
  not not_5 (not_5_out, S3);
  not not_6 (not_6_out, S1);
  not not_7 (not_7_out, S0);
  not not_8 (N0, S0);
  and and_1 (and_1_out, S2, S1, S0);
  and and_2 (and_2_out, S3, not_1_out);
  and and_3 (and_3_out, S3, S1);
  and and_4 (and_4_out, S3, S2);
  and and_5 (and_5_out, not_2_out, S1, S0);
  and and_6 (and_6_out, S2, not_3_out);
  and and_7 (and_7_out, S2, not_4_out);
  and and_8 (and_8_out, not_5_out, not_6_out, S0);
  and and_9 (and_9_out, S1, not_7_out);
  or or_1 (N3, and_1_out, and_2_out, and_3_out, and_4_out);
  or or_2 (N2, and_5_out, and_6_out, and_7_out);
  or or_3 (N1, and_8_out, and_9_out);

  // Notes on the sheet:
  //   Input states
  //   Output states
endmodule

module _4_bit_BCD_Counter_Output_Circuit (
  input  S3,
  input  S2,
  input  S1,
  input  S0,
  output Carryout
);

  wire not_1_out, not_2_out;

  not not_1 (not_1_out, S2);
  not not_2 (not_2_out, S1);
  and and_1 (Carryout, S3, not_1_out, not_2_out, S0);

  // Notes on the sheet:
  //   Input states
  //   Output
endmodule

module _4_bit_BCD_Counter (
  input  CLK,
  input  Enable,
  input  Reset,
  output [3:0] Output,
  output Carryout
);

  wire n4_bit_bcd_counter_state_transition_circuit_1_n0, n4_bit_bcd_counter_state_transition_circuit_1_n1,
       n4_bit_bcd_counter_state_transition_circuit_1_n2, n4_bit_bcd_counter_state_transition_circuit_1_n3;

  D_Flip_Flop d_ff_1 (
    .clk(CLK), .D(n4_bit_bcd_counter_state_transition_circuit_1_n3), .Q(Output[3]), .en(Enable), .reset(Reset));  // open: Qn, preset
  D_Flip_Flop d_ff_2 (
    .clk(CLK), .D(n4_bit_bcd_counter_state_transition_circuit_1_n2), .Q(Output[2]), .en(Enable), .reset(Reset));  // open: Qn, preset
  D_Flip_Flop d_ff_3 (
    .clk(CLK), .D(n4_bit_bcd_counter_state_transition_circuit_1_n1), .Q(Output[1]), .en(Enable), .reset(Reset));  // open: Qn, preset
  D_Flip_Flop d_ff_4 (
    .clk(CLK), .D(n4_bit_bcd_counter_state_transition_circuit_1_n0), .Q(Output[0]), .en(Enable), .reset(Reset));  // open: Qn, preset
  _4_bit_BCD_Counter_Output_Circuit u_4_bit_bcd_counter_output_circuit_1 (
    .S3(Output[3]), .S2(Output[2]), .S1(Output[1]), .Carryout(Carryout), .S0(Output[0]));
  _4_bit_BCD_Counter_State_Transition_Circuit u_4_bit_bcd_counter_state_transition_circuit_1 (
    .S3(Output[3]), .N3(n4_bit_bcd_counter_state_transition_circuit_1_n3), .S2(Output[2]),
    .N2(n4_bit_bcd_counter_state_transition_circuit_1_n2), .S1(Output[1]),
    .N1(n4_bit_bcd_counter_state_transition_circuit_1_n1), .S0(Output[0]),
    .N0(n4_bit_bcd_counter_state_transition_circuit_1_n0));

  // Notes on the sheet:
  //   Function: 
  //   Input
  //   "Carryout" is 1 only when "Output" is 1001 
  //   If "Reset" is 1, the register is reset to 0 asynchronously
  //   If "Enable" is 0, the CLK triggers will be ineffective
  //   At the CLK rising edge, the "Output" will increase by one. The Output will count cycly in the range of 0000 - 1001
  //   Output
endmodule

module _4_digit_BCD_Counter (
  input  CLK,
  input  Enable,
  input  Reset,
  output [15:0] Output
);

  wire and_1_out, and_2_out, clock_1_out, n4_bit_bcd_counter_2_carryout, n4_bit_bcd_counter_3_carryout,
       n4_bit_bcd_counter_4_carryout, n7_segment_display_control_1_output0,
       n7_segment_display_control_1_output1, n7_segment_display_control_1_output2,
       n7_segment_display_control_1_output3, n7_segment_display_control_1_output4,
       n7_segment_display_control_1_output5, n7_segment_display_control_1_output6,
       n7_segment_display_control_2_output0, n7_segment_display_control_2_output1,
       n7_segment_display_control_2_output2, n7_segment_display_control_2_output3,
       n7_segment_display_control_2_output4, n7_segment_display_control_2_output5,
       n7_segment_display_control_2_output6, n7_segment_display_control_3_output0,
       n7_segment_display_control_3_output1, n7_segment_display_control_3_output2,
       n7_segment_display_control_3_output3, n7_segment_display_control_3_output4,
       n7_segment_display_control_3_output5, n7_segment_display_control_3_output6,
       n7_segment_display_control_4_output0, n7_segment_display_control_4_output1,
       n7_segment_display_control_4_output2, n7_segment_display_control_4_output3,
       n7_segment_display_control_4_output4, n7_segment_display_control_4_output5,
       n7_segment_display_control_4_output6, Output0, Output1, Output2, Output3, Output4, Output5, Output6;

  Clock clock_1 (.out(clock_1_out));
  _7_Segment_Display u_7_segment_display_1 (
    .g(n7_segment_display_control_1_output0), .f(n7_segment_display_control_1_output1),
    .a(n7_segment_display_control_1_output2), .b(n7_segment_display_control_1_output3),
    .e(n7_segment_display_control_1_output6), .d(n7_segment_display_control_1_output5),
    .c(n7_segment_display_control_1_output4));  // open: dp
  _7_Segment_Display_Control u_7_segment_display_control_1 (
    .Input0(Output[12]), .Output0(n7_segment_display_control_1_output0),
    .Output4(n7_segment_display_control_1_output4), .Input1(Output[13]),
    .Output1(n7_segment_display_control_1_output1), .Output5(n7_segment_display_control_1_output5),
    .Input2(Output[14]), .Output2(n7_segment_display_control_1_output2),
    .Output6(n7_segment_display_control_1_output6), .Input3(Output[15]),
    .Output3(n7_segment_display_control_1_output3));
  _4_bit_BCD_Counter u_4_bit_bcd_counter_1 (
    .CLK(clock_1_out), .Output(Output[15:12]), .Enable(and_1_out), .Reset(Reset));  // open: Carryout
  and and_1 (and_1_out, n4_bit_bcd_counter_2_carryout, and_2_out);
  _7_Segment_Display u_7_segment_display_2 (
    .g(n7_segment_display_control_2_output0), .f(n7_segment_display_control_2_output1),
    .a(n7_segment_display_control_2_output2), .b(n7_segment_display_control_2_output3),
    .e(n7_segment_display_control_2_output6), .d(n7_segment_display_control_2_output5),
    .c(n7_segment_display_control_2_output4));  // open: dp
  _7_Segment_Display_Control u_7_segment_display_control_2 (
    .Input0(Output[8]), .Output0(n7_segment_display_control_2_output0),
    .Output4(n7_segment_display_control_2_output4), .Input1(Output[9]),
    .Output1(n7_segment_display_control_2_output1), .Output5(n7_segment_display_control_2_output5),
    .Input2(Output[10]), .Output2(n7_segment_display_control_2_output2),
    .Output6(n7_segment_display_control_2_output6), .Input3(Output[11]),
    .Output3(n7_segment_display_control_2_output3));
  _4_bit_BCD_Counter u_4_bit_bcd_counter_2 (
    .CLK(clock_1_out), .Output(Output[11:8]), .Enable(and_2_out), .Reset(Reset),
    .Carryout(n4_bit_bcd_counter_2_carryout));
  and and_2 (and_2_out, n4_bit_bcd_counter_3_carryout, n4_bit_bcd_counter_4_carryout);
  _7_Segment_Display_Control u_7_segment_display_control_3 (
    .Input0(Output[4]), .Output0(n7_segment_display_control_3_output0),
    .Output4(n7_segment_display_control_3_output4), .Input1(Output[5]),
    .Output1(n7_segment_display_control_3_output1), .Output5(n7_segment_display_control_3_output5),
    .Input2(Output[6]), .Output2(n7_segment_display_control_3_output2),
    .Output6(n7_segment_display_control_3_output6), .Input3(Output[7]),
    .Output3(n7_segment_display_control_3_output3));
  _4_bit_BCD_Counter u_4_bit_bcd_counter_3 (
    .CLK(clock_1_out), .Output(Output[7:4]), .Enable(n4_bit_bcd_counter_4_carryout), .Reset(Reset),
    .Carryout(n4_bit_bcd_counter_3_carryout));
  _7_Segment_Display u_7_segment_display_3 (
    .g(n7_segment_display_control_3_output0), .f(n7_segment_display_control_3_output1),
    .a(n7_segment_display_control_3_output2), .b(n7_segment_display_control_3_output3),
    .e(n7_segment_display_control_3_output6), .d(n7_segment_display_control_3_output5),
    .c(n7_segment_display_control_3_output4));  // open: dp
  _7_Segment_Display_Control u_7_segment_display_control_4 (
    .Input0(Output[0]), .Output0(n7_segment_display_control_4_output0),
    .Output4(n7_segment_display_control_4_output4), .Input1(Output[1]),
    .Output1(n7_segment_display_control_4_output1), .Output5(n7_segment_display_control_4_output5),
    .Input2(Output[2]), .Output2(n7_segment_display_control_4_output2),
    .Output6(n7_segment_display_control_4_output6), .Input3(Output[3]),
    .Output3(n7_segment_display_control_4_output3));
  _4_bit_BCD_Counter u_4_bit_bcd_counter_4 (
    .CLK(clock_1_out), .Output(Output[3:0]), .Enable(Enable), .Reset(Reset),
    .Carryout(n4_bit_bcd_counter_4_carryout));
  _7_Segment_Display u_7_segment_display_4 (
    .g(Output0), .f(Output1), .a(Output2), .b(Output3), .e(Output6), .d(Output5), .c(Output4), .dp(1'b1));
  _7_Segment_Display u_7_segment_display_5 (
    .g(n7_segment_display_control_4_output0), .f(n7_segment_display_control_4_output1),
    .a(n7_segment_display_control_4_output2), .b(n7_segment_display_control_4_output3),
    .e(n7_segment_display_control_4_output6), .d(n7_segment_display_control_4_output5),
    .c(n7_segment_display_control_4_output4));  // open: dp

  // Notes on the sheet:
  //   Function: 
  //   Input
  //   At the CLK rising edge, the "Output" will increase by one.
  //   If "Reset" is 1, the register is reset to 0 asynchronously
  //   If "Enable" is 0, the CLK triggers will be ineffective
  //   4-digit BCD counter. Each 4-bit is used to represent the value of one decimal digit.
  //   Output
endmodule

module Stopwatch_State_Transition_Control (
  input  Start,
  input  Stop,
  input  Store,
  input  Reset,
  input  NewRecordFlag,
  input  S2,
  input  S1,
  input  S0,
  output N2,
  output N1,
  output N0
);

  wire and_1_out, and_2_out, and_3_out, and_4_out, and_5_out, and_6_out, and_7_out, and_8_out, and_9_out,
       and_10_out, and_11_out, and_12_out, and_13_out, and_14_out, and_15_out, and_16_out, and_17_out,
       and_18_out, and_19_out, not_1_out, not_2_out, not_3_out, not_4_out, not_5_out, not_6_out, not_7_out,
       not_8_out, not_9_out, not_10_out, not_11_out, not_12_out, not_13_out, not_14_out, not_15_out,
       not_16_out, not_17_out, not_18_out, not_19_out, not_20_out, not_21_out, not_22_out, not_23_out,
       not_24_out, not_25_out, not_26_out, not_27_out, not_28_out, not_29_out, not_30_out, not_31_out,
       not_32_out, not_33_out, not_34_out, not_35_out, not_36_out;

  not not_1 (not_1_out, Start);
  not not_2 (not_2_out, Stop);
  and and_1 (and_1_out, not_1_out, not_2_out, S2);
  not not_3 (not_3_out, Start);
  and and_2 (and_2_out, not_3_out, Store);
  and and_3 (and_3_out, Stop, Store);
  not not_4 (not_4_out, Start);
  not not_5 (not_5_out, Store);
  not not_6 (not_6_out, Store);
  not not_7 (not_7_out, Stop);
  not not_8 (not_8_out, S2);
  not not_9 (not_9_out, S1);
  not not_10 (not_10_out, Stop);
  not not_11 (not_11_out, S2);
  not not_12 (not_12_out, S0);
  not not_13 (not_13_out, Start);
  not not_14 (not_14_out, Reset);
  not not_15 (not_15_out, NewRecordFlag);
  not not_16 (not_16_out, Start);
  not not_17 (not_17_out, Reset);
  not not_18 (not_18_out, S1);
  not not_19 (not_19_out, Store);
  not not_20 (not_20_out, Reset);
  not not_21 (not_21_out, Reset);
  not not_22 (not_22_out, Start);
  not not_23 (not_23_out, Reset);
  not not_24 (not_24_out, S0);
  not not_25 (not_25_out, Reset);
  not not_26 (not_26_out, NewRecordFlag);
  not not_27 (not_27_out, Reset);
  not not_28 (not_28_out, S1);
  not not_29 (not_29_out, Reset);
  not not_30 (not_30_out, S0);
  not not_31 (not_31_out, Reset);
  not not_32 (not_32_out, S1);
  not not_33 (not_33_out, S0);
  not not_34 (not_34_out, Stop);
  not not_35 (not_35_out, Reset);
  not not_36 (not_36_out, Reset);
  or or_1 (N2, and_1_out, Reset, and_2_out, and_3_out);
  and and_4 (and_4_out, not_4_out, not_5_out, S1);
  and and_5 (and_5_out, Stop, not_6_out);
  and and_6 (and_6_out, Start, not_7_out, not_8_out, not_9_out, S0);
  and and_7 (and_7_out, Start, not_10_out, not_11_out, S1, not_12_out);
  and and_8 (and_8_out, not_13_out, not_14_out, not_15_out, S0);
  and and_9 (and_9_out, not_16_out, not_17_out, not_18_out, S0);
  and and_10 (and_10_out, not_19_out, not_20_out, S1, S0);
  and and_11 (and_11_out, not_21_out, S2, S0);
  and and_12 (and_12_out, Reset, S2, S1);
  and and_13 (and_13_out, not_22_out, Store, not_23_out, not_24_out);
  and and_14 (and_14_out, Stop, not_25_out, not_26_out);
  and and_15 (and_15_out, Stop, not_27_out, not_28_out);
  and and_16 (and_16_out, Stop, not_29_out, not_30_out);
  and and_17 (and_17_out, Start, not_31_out, not_32_out, not_33_out);
  and and_18 (and_18_out, Start, not_34_out, not_35_out, S1, S0);
  and and_19 (and_19_out, Start, not_36_out, S2);
  or or_2 (N1, and_4_out, Reset, and_5_out, and_6_out, and_7_out);
  or or_3 (N0, and_8_out, and_9_out, and_10_out, and_11_out, and_12_out, and_13_out, and_14_out, and_15_out, and_16_out, and_17_out, and_18_out, and_19_out);
endmodule

module Stopwatch_Output_Control (
  input  S2,
  input  S1,
  input  S0,
  output DisplayInputSel,
  output CounterEN,
  output RegisterEN,
  output CounterReset,
  output RegisterInputSel
);

  wire and_1_out, and_2_out, and_3_out, and_4_out, and_5_out, and_6_out, not_1_out, not_2_out, not_3_out,
       not_4_out, not_5_out, not_6_out, not_7_out, not_8_out, not_9_out, not_10_out, not_11_out;

  not not_1 (not_1_out, S2);
  not not_2 (not_2_out, S0);
  not not_3 (not_3_out, S2);
  not not_4 (not_4_out, S1);
  not not_5 (not_5_out, S2);
  not not_6 (not_6_out, S0);
  not not_7 (not_7_out, S1);
  not not_8 (not_8_out, S0);
  not not_9 (not_9_out, S2);
  not not_10 (not_10_out, S1);
  not not_11 (not_11_out, S1);
  or or_1 (DisplayInputSel, not_1_out, not_2_out, S1);
  and and_1 (and_1_out, not_3_out, not_4_out, S0);
  and and_2 (and_2_out, not_5_out, S1, not_6_out);
  and and_3 (and_3_out, S2, not_7_out, not_8_out);
  and and_4 (and_4_out, S2, S1, S0);
  and and_5 (and_5_out, not_9_out, not_10_out);
  and and_6 (and_6_out, S2, S1);
  and and_7 (RegisterInputSel, S2, not_11_out);
  or or_2 (CounterEN, and_1_out, and_2_out);
  or or_3 (RegisterEN, and_3_out, and_4_out);
  or or_4 (CounterReset, and_5_out, and_6_out);

  // Notes on the sheet:
  //   Previous states
  //   Outputs
endmodule

module Stopwatch_Control_Unit (
  input  Start,
  input  Reset,
  input  Stop,
  input  NewRecordFlag,
  input  Store,
  input  CLK,
  output DisplayInputSel,
  output CounterEN,
  output RegisterEN,
  output CounterReset,
  output RegisterInputSel
);

  wire d_ff_1_q, d_ff_2_q, d_ff_3_q, stopwatch_state_transition_control_1_n0,
       stopwatch_state_transition_control_1_n1, stopwatch_state_transition_control_1_n2;

  Stopwatch_State_Transition_Control stopwatch_state_transition_control_1 (
    .Start(Start), .Stop(Stop), .N2(stopwatch_state_transition_control_1_n2), .Store(Store), .Reset(Reset),
    .NewRecordFlag(NewRecordFlag), .S2(d_ff_1_q), .N1(stopwatch_state_transition_control_1_n1),
    .S1(d_ff_2_q), .S0(d_ff_3_q), .N0(stopwatch_state_transition_control_1_n0));
  Stopwatch_Output_Control stopwatch_output_control_1 (
    .DisplayInputSel(DisplayInputSel), .RegisterEN(RegisterEN), .S2(d_ff_1_q), .S1(d_ff_2_q),
    .RegisterInputSel(RegisterInputSel), .S0(d_ff_3_q), .CounterEN(CounterEN), .CounterReset(CounterReset));
  D_Flip_Flop d_ff_1 (
    .clk(CLK), .D(stopwatch_state_transition_control_1_n2), .Q(d_ff_1_q));  // open: Qn, preset, en, reset
  D_Flip_Flop d_ff_2 (
    .clk(CLK), .D(stopwatch_state_transition_control_1_n1), .Q(d_ff_2_q));  // open: Qn, preset, en, reset
  D_Flip_Flop d_ff_3 (
    .clk(CLK), .D(stopwatch_state_transition_control_1_n0), .Q(d_ff_3_q));  // open: Qn, preset, en, reset

  // Notes on the sheet:
  //   Inputs
  //   Outputs
endmodule

module StopWatch (
);

  wire CLK_out, CounterEN, CounterReset, DisplayInputSel, NewRecordFlag, RegisterEN, RegisterInputSel, Reset,
       Start, Stop, Store;
  wire [2:0] DP1_2, DP2_2, DP3_2, DP4_2;
  wire [3:0] DP1_1, DP2_1, DP3_1, DP4_1, n2_channel_16_bit_multiplexer_2_output,
       n2_channel_16_bit_multiplexer_2_output_2, n2_channel_16_bit_multiplexer_2_output_3,
       n2_channel_16_bit_multiplexer_2_output_4;
  wire [15:0] n2_channel_16_bit_multiplexer_1_output, n4_digit_bcd_counter_1_output,
       n16_bit_parallel_load_register_1_output;

  Button u_Start (.out(Start));
  Button u_Stop (.out(Stop));
  Button u_Store (.out(Store));
  Button u_Reset (.out(Reset));
  _7_Segment_Display_Control u_7_segment_display_control_1 (
    .Input0(n2_channel_16_bit_multiplexer_2_output_4[0]), .Output0(DP4_1[0]), .Output4(DP4_2[0]),
    .Input1(n2_channel_16_bit_multiplexer_2_output_4[1]), .Output1(DP4_1[1]), .Output5(DP4_2[1]),
    .Input2(n2_channel_16_bit_multiplexer_2_output_4[2]), .Output2(DP4_1[2]), .Output6(DP4_2[2]),
    .Input3(n2_channel_16_bit_multiplexer_2_output_4[3]), .Output3(DP4_1[3]));
  _7_Segment_Display u_7_segment_display_1 (
    .g(DP4_1[0]), .f(DP4_1[1]), .a(DP4_1[2]), .b(DP4_1[3]), .e(DP4_2[2]), .d(DP4_2[1]), .c(DP4_2[0]));  // open: dp
  _2_channel_16_bit_multiplexer u_2_channel_16_bit_multiplexer_1 (
    .Input0(16'h9999), .Output(n2_channel_16_bit_multiplexer_1_output),
    .Input1(n4_digit_bcd_counter_1_output), .Sel(RegisterInputSel));
  _7_Segment_Display u_7_segment_display_2 (
    .g(DP2_1[0]), .f(DP2_1[1]), .a(DP2_1[2]), .b(DP2_1[3]), .e(DP2_2[2]), .d(DP2_2[1]), .c(DP2_2[0]));  // open: dp
  _7_Segment_Display u_7_segment_display_3 (
    .g(DP3_1[0]), .f(DP3_1[1]), .a(DP3_1[2]), .b(DP3_1[3]), .e(DP3_2[2]), .d(DP3_2[1]), .c(DP3_2[0]),
    .dp(1'b1));
  _7_Segment_Display_Control u_7_segment_display_control_2 (
    .Input0(n2_channel_16_bit_multiplexer_2_output_3[0]), .Output0(DP3_1[0]), .Output4(DP3_2[0]),
    .Input1(n2_channel_16_bit_multiplexer_2_output_3[1]), .Output1(DP3_1[1]), .Output5(DP3_2[1]),
    .Input2(n2_channel_16_bit_multiplexer_2_output_3[2]), .Output2(DP3_1[2]), .Output6(DP3_2[2]),
    .Input3(n2_channel_16_bit_multiplexer_2_output_3[3]), .Output3(DP3_1[3]));
  _16_bit_Parallel_load_register u_16_bit_parallel_load_register_1 (
    .Input(n2_channel_16_bit_multiplexer_1_output), .Output(n16_bit_parallel_load_register_1_output),
    .Enable(RegisterEN), .CLK(CLK_out));  // open: Reset
  _7_Segment_Display u_7_segment_display_4 (
    .g(DP1_1[0]), .f(DP1_1[1]), .a(DP1_1[2]), .b(DP1_1[3]), .e(DP1_2[2]), .d(DP1_2[1]), .c(DP1_2[0]));  // open: dp
  _2_channel_16_bit_multiplexer u_2_channel_16_bit_multiplexer_2 (
    .Input0(n16_bit_parallel_load_register_1_output),
    .Output({n2_channel_16_bit_multiplexer_2_output_4, n2_channel_16_bit_multiplexer_2_output_3, n2_channel_16_bit_multiplexer_2_output_2, n2_channel_16_bit_multiplexer_2_output}),
    .Input1(n4_digit_bcd_counter_1_output), .Sel(DisplayInputSel));
  _16_bit_unsigned_comparator u_16_bit_unsigned_comparator_1 (
    .a(n4_digit_bcd_counter_1_output), .Less(NewRecordFlag), .b(n16_bit_parallel_load_register_1_output));  // open: Greater, Equal
  _7_Segment_Display_Control u_7_segment_display_control_3 (
    .Input0(n2_channel_16_bit_multiplexer_2_output_2[0]), .Output0(DP2_1[0]), .Output4(DP2_2[0]),
    .Input1(n2_channel_16_bit_multiplexer_2_output_2[1]), .Output1(DP2_1[1]), .Output5(DP2_2[1]),
    .Input2(n2_channel_16_bit_multiplexer_2_output_2[2]), .Output2(DP2_1[2]), .Output6(DP2_2[2]),
    .Input3(n2_channel_16_bit_multiplexer_2_output_2[3]), .Output3(DP2_1[3]));
  _4_digit_BCD_Counter u_4_digit_bcd_counter_1 (
    .Output(n4_digit_bcd_counter_1_output), .Enable(CounterEN), .Reset(CounterReset), .CLK(CLK_out));
  _7_Segment_Display_Control u_7_segment_display_control_4 (
    .Input0(n2_channel_16_bit_multiplexer_2_output[0]), .Output0(DP1_1[0]), .Output4(DP1_2[0]),
    .Input1(n2_channel_16_bit_multiplexer_2_output[1]), .Output1(DP1_1[1]), .Output5(DP1_2[1]),
    .Input2(n2_channel_16_bit_multiplexer_2_output[2]), .Output2(DP1_1[2]), .Output6(DP1_2[2]),
    .Input3(n2_channel_16_bit_multiplexer_2_output[3]), .Output3(DP1_1[3]));
  Stopwatch_Control_Unit stopwatch_control_unit_1 (
    .Start(Start), .CLK(CLK_out), .DisplayInputSel(DisplayInputSel), .Stop(Stop), .RegisterEN(RegisterEN),
    .Store(Store), .RegisterInputSel(RegisterInputSel), .Reset(Reset), .CounterEN(CounterEN),
    .NewRecordFlag(NewRecordFlag), .CounterReset(CounterReset));
  Clock #(.highDuration(5), .lowDuration(5)) CLK (.out(CLK_out));
endmodule

module extra (
  input  S2,
  input  S1,
  input  S0,
  output DisplayInputSel,
  output CounterEN,
  output RegisterEN,
  output CounterReset,
  output RegisterInputSel
);

  wire and_1_out, and_2_out, and_3_out, and_4_out, and_5_out, and_6_out, not_1_out, not_2_out, not_3_out,
       not_4_out, not_5_out, not_6_out, not_7_out, not_8_out, not_9_out, not_10_out, not_11_out;

  not not_1 (not_1_out, S2);
  not not_2 (not_2_out, S0);
  not not_3 (not_3_out, S2);
  not not_4 (not_4_out, S1);
  not not_5 (not_5_out, S2);
  not not_6 (not_6_out, S0);
  not not_7 (not_7_out, S1);
  not not_8 (not_8_out, S0);
  not not_9 (not_9_out, S2);
  not not_10 (not_10_out, S1);
  not not_11 (not_11_out, S1);
  or or_1 (DisplayInputSel, not_1_out, not_2_out, S1);
  and and_1 (and_1_out, not_3_out, not_4_out, S0);
  and and_2 (and_2_out, not_5_out, S1, not_6_out);
  and and_3 (and_3_out, S2, not_7_out, not_8_out);
  and and_4 (and_4_out, S2, S1, S0);
  and and_5 (and_5_out, not_9_out, not_10_out);
  and and_6 (and_6_out, S2, S1);
  and and_7 (RegisterInputSel, S2, not_11_out);
  or or_2 (CounterEN, and_1_out, and_2_out);
  or or_3 (RegisterEN, and_3_out, and_4_out);
  or or_4 (CounterReset, and_5_out, and_6_out);
endmodule
