// Logisim project Lab2 - ALU.circ as structural Verilog: 10 circuits, main circuit 32-bit ALU
module _1_bit_full_adder (
  input  a,
  input  CarryIn,
  input  b,
  output S,
  output CarryOut
);

  wire and_1_out, and_2_out, xor_1_out;

  xor xor_1 (xor_1_out, a, b);
  xor xor_2 (S, xor_1_out, CarryIn);
  and and_1 (and_1_out, xor_1_out, CarryIn);
  and and_2 (and_2_out, a, b);
  or or_1 (CarryOut, and_1_out, and_2_out);

  // Notes on the sheet:
  //   Function: S = a XOR b XOR CarryIn
  //   Input
  //   CarryOut = ab + CarryIn(a XOR b)  
  //   Output
endmodule

module _8_bit_Ripple_Carry_Adder_and_Subtracter (
  input  [7:0] a,
  input  [7:0] b,
  input  Sub,
  output [7:0] S,
  output CarryOut,
  output Overflow
);

  wire n1_bit_full_adder_2_carryout, n1_bit_full_adder_3_carryout, n1_bit_full_adder_4_carryout,
       n1_bit_full_adder_5_carryout, n1_bit_full_adder_6_carryout, n1_bit_full_adder_7_carryout,
       n1_bit_full_adder_8_carryout, xor_2_out, xor_3_out, xor_4_out, xor_5_out, xor_6_out, xor_7_out,
       xor_8_out, xor_9_out, xor_10_out;

  xor xor_1 (Overflow, n1_bit_full_adder_2_carryout, CarryOut);
  _1_bit_full_adder u_1_bit_full_adder_1 (
    .a(a[7]), .b(xor_2_out), .CarryIn(n1_bit_full_adder_2_carryout), .CarryOut(CarryOut), .S(S[7]));
  xor xor_2 (xor_2_out, b[7], Sub);
  _1_bit_full_adder u_1_bit_full_adder_2 (
    .a(a[6]), .b(xor_3_out), .CarryIn(n1_bit_full_adder_3_carryout), .CarryOut(n1_bit_full_adder_2_carryout),
    .S(S[6]));
  xor xor_3 (xor_3_out, b[6], Sub);
  _1_bit_full_adder u_1_bit_full_adder_3 (
    .a(a[5]), .b(xor_4_out), .CarryIn(n1_bit_full_adder_4_carryout), .CarryOut(n1_bit_full_adder_3_carryout),
    .S(S[5]));
  xor xor_4 (xor_4_out, b[5], Sub);
  _1_bit_full_adder u_1_bit_full_adder_4 (
    .a(a[4]), .b(xor_5_out), .CarryIn(n1_bit_full_adder_5_carryout), .CarryOut(n1_bit_full_adder_4_carryout),
    .S(S[4]));
  xor xor_5 (xor_5_out, b[4], Sub);
  _1_bit_full_adder u_1_bit_full_adder_5 (
    .a(a[3]), .b(xor_6_out), .CarryIn(n1_bit_full_adder_6_carryout), .CarryOut(n1_bit_full_adder_5_carryout),
    .S(S[3]));
  xor xor_6 (xor_6_out, b[3], Sub);
  _1_bit_full_adder u_1_bit_full_adder_6 (
    .a(a[2]), .b(xor_7_out), .CarryIn(n1_bit_full_adder_7_carryout), .CarryOut(n1_bit_full_adder_6_carryout),
    .S(S[2]));
  xor xor_7 (xor_7_out, b[2], Sub);
  _1_bit_full_adder u_1_bit_full_adder_7 (
    .a(a[1]), .b(xor_8_out), .CarryIn(n1_bit_full_adder_8_carryout), .CarryOut(n1_bit_full_adder_7_carryout),
    .S(S[1]));
  xor xor_8 (xor_8_out, b[1], Sub);
  // Probe on a
  // Probe on b
  // Probe on S
  _1_bit_full_adder u_1_bit_full_adder_8 (
    .a(a[0]), .b(xor_9_out), .CarryIn(xor_10_out), .CarryOut(n1_bit_full_adder_8_carryout), .S(S[0]));
  xor xor_9 (xor_9_out, b[0], Sub);
  xor xor_10 (xor_10_out, 1'b0, Sub);
  // Probe on a
  // Probe on b
  // Probe on S

  // Notes on the sheet:
  //   Input
  //   Note: If Sub = 0: Sum = a + b; If Sub = 1: Sum = a - b; 
  //   Output
  //   Unsigned Result
  //   Signed Result
endmodule

module _4_bit_Carry_Lookahead_Unit (
  input  g3,
  input  g2,
  input  g1,
  input  g0,
  input  p3,
  input  p2,
  input  p1,
  input  p0,
  input  C0,
  output C4,
  output C3,
  output C2,
  output C1,
  output G,
  output P
);

  wire and_1_out, and_2_out, and_3_out, and_4_out, and_5_out, and_6_out, and_7_out, and_8_out, and_9_out,
       and_10_out, and_11_out, and_12_out, and_13_out;

  and and_1 (and_1_out, p3, g2);
  and and_2 (and_2_out, p3, p2, g1);
  and and_3 (and_3_out, p2, g1);
  and and_4 (and_4_out, p2, p1, g0);
  and and_5 (and_5_out, p3, g2);
  and and_6 (and_6_out, p3, p2, g1);
  and and_7 (and_7_out, p3, p2, p1, g0);
  and and_8 (and_8_out, p3, p2, p1, p0, C0);
  and and_9 (and_9_out, p3, p2, p1, g0);
  and and_10 (and_10_out, p0, C0);
  and and_11 (and_11_out, p1, g0);
  and and_12 (and_12_out, p1, p0, C0);
  and and_13 (and_13_out, p2, p1, p0, C0);
  and and_14 (P, p0, p1, p2, p3);
  or or_1 (G, g3, and_1_out, and_2_out, and_9_out);
  or or_2 (C1, g0, and_10_out);
  or or_3 (C2, g1, and_11_out, and_12_out);
  or or_4 (C3, g2, and_3_out, and_4_out, and_13_out);
  or or_5 (C4, g3, and_5_out, and_6_out, and_7_out, and_8_out);

  // Notes on the sheet:
  //   Input
  //   Note: Please reference the lecture slides to understand the meaning of inputs and outputs.
  //   P = p3 * p2 * p1 * p0
  //   G = g3 + (p3 * g2) + (p3 * p2 * g1) + (p3 * p2 * p1 * g0)
  //   C1 = g0 + (p0 * c0)
  //   C2 = g1 + (p1 * g0) + (p1 * p0 * c0)
  //   C3 = g2 + (p2 * g1) + (p2 * p1 * g0) + (p2 * p1 * p0 * c0)
  //   C4 = g3 + (p3 * g2) + (p3 * p2 * g1) + (p3 * p2 * p1 * g0) + (p3 * p2 * p1 * p0 * c0)
  //   Output
endmodule

module _4_bit_Carry_Lookahead_Adder (
  input  [3:0] a,
  input  [3:0] b,
  input  C0,
  output [3:0] S,
  output C4,
  output C3,
  output G,
  output P
);

  wire and_1_out, and_2_out, and_3_out, and_4_out, n4_bit_carry_lookahead_unit_1_c1,
       n4_bit_carry_lookahead_unit_1_c2, n4_bit_carry_lookahead_unit_1_c3, or_1_out, or_2_out, or_3_out,
       or_4_out;

  and and_1 (and_1_out, a[3], b[3]);
  _1_bit_full_adder u_1_bit_full_adder_1 (
    .a(a[3]), .b(b[3]), .CarryIn(n4_bit_carry_lookahead_unit_1_c3), .CarryOut(C3), .S(S[3]));
  and and_2 (and_2_out, a[2], b[2]);
  or or_1 (or_1_out, a[3], b[3]);
  _1_bit_full_adder u_1_bit_full_adder_2 (
    .a(a[2]), .b(b[2]), .CarryIn(n4_bit_carry_lookahead_unit_1_c2), .S(S[2]));  // open: CarryOut
  or or_2 (or_2_out, a[2], b[2]);
  _4_bit_Carry_Lookahead_Unit u_4_bit_carry_lookahead_unit_1 (
    .g3(and_1_out), .g2(and_2_out), .g1(and_3_out), .g0(and_4_out), .p3(or_1_out), .p2(or_2_out),
    .p1(or_3_out), .p0(or_4_out), .C0(C0), .C4(C4), .C3(n4_bit_carry_lookahead_unit_1_c3),
    .C2(n4_bit_carry_lookahead_unit_1_c2), .C1(n4_bit_carry_lookahead_unit_1_c1), .G(G), .P(P));
  and and_3 (and_3_out, a[1], b[1]);
  _1_bit_full_adder u_1_bit_full_adder_3 (
    .a(a[1]), .b(b[1]), .CarryIn(n4_bit_carry_lookahead_unit_1_c1), .S(S[1]));  // open: CarryOut
  and and_4 (and_4_out, a[0], b[0]);
  or or_3 (or_3_out, a[1], b[1]);
  // Probe on a
  // Probe on b
  // Probe on S
  _1_bit_full_adder u_1_bit_full_adder_4 (.a(a[0]), .b(b[0]), .CarryIn(C0), .S(S[0]));  // open: CarryOut
  or or_4 (or_4_out, a[0], b[0]);
  // Probe on a
  // Probe on b
  // Probe on S

  // Notes on the sheet:
  //   Input
  //   Note: Please reference the lecture slides to understand the meaning of inputs and outputs.
  //   Output
  //   +
  //   =
  //   Unsigned Result
  //   +
  //   =
  //   Signed Result
endmodule

module _16_bit_Carry_Lookahead_Adder (
  input  [15:0] a,
  input  [15:0] b,
  input  C0,
  output [15:0] S,
  output C16,
  output C15,
  output G,
  output P
);

  wire g0, g1, g2, g3, n4_bit_carry_lookahead_unit_1_c1, n4_bit_carry_lookahead_unit_1_c2, p0, p1, p2, p3;

  _4_bit_Carry_Lookahead_Adder u_4_bit_carry_lookahead_adder_1 (
    .a(a[15:12]), .b(b[15:12]), .C0(C15), .S(S[15:12]), .G(g3), .P(p3));  // open: C4, C3
  _4_bit_Carry_Lookahead_Unit u_4_bit_carry_lookahead_unit_1 (
    .g3(g3), .g2(g2), .g1(g1), .g0(g0), .p3(p3), .p2(p2), .p1(p1), .p0(p0), .C0(C0), .C4(C16), .C3(C15),
    .C2(n4_bit_carry_lookahead_unit_1_c2), .C1(n4_bit_carry_lookahead_unit_1_c1), .G(G), .P(P));
  _4_bit_Carry_Lookahead_Adder u_4_bit_carry_lookahead_adder_2 (
    .a(a[11:8]), .b(b[11:8]), .C0(n4_bit_carry_lookahead_unit_1_c2), .S(S[11:8]), .G(g2), .P(p2));  // open: C4, C3
  _4_bit_Carry_Lookahead_Adder u_4_bit_carry_lookahead_adder_3 (
    .a(a[7:4]), .b(b[7:4]), .C0(n4_bit_carry_lookahead_unit_1_c1), .S(S[7:4]), .G(g1), .P(p1));  // open: C4, C3
  // Probe on a
  // Probe on b
  // Probe on S
  _4_bit_Carry_Lookahead_Adder u_4_bit_carry_lookahead_adder_4 (
    .a(a[3:0]), .b(b[3:0]), .C0(C0), .S(S[3:0]), .G(g0), .P(p0));  // open: C4, C3
  // Probe on a
  // Probe on b
  // Probe on S

  // Other names for the same wires on the sheet: a0[3:0] = a[3:0]; a1[3:0] = a[7:4]; a2[3:0] = a[11:8];
  //   a3[3:0] = a[15:12]; b0[3:0] = b[3:0]; b1[3:0] = b[7:4]; b2[3:0] = b[11:8]; b3[3:0] = b[15:12]; S0[3:0] = S[3:0];
  //   S1[3:0] = S[7:4]; S2[3:0] = S[11:8]; S3[3:0] = S[15:12]

  // Notes on the sheet:
  //   Input
  //   Note: Please reference the lecture slides to understand the meaning of inputs and outputs.
  //   Output
  //   +
  //   =
  //   Unsigned Result
  //   +
  //   =
  //   Signed Result
endmodule

module _32_bit_Carry_Lookahead_Adder (
  input  [31:0] a,
  input  [31:0] b,
  input  C0,
  output C32,
  output C31,
  output [31:0] S
);

  wire n16_bit_carry_lookahead_adder_2_c16;

  _16_bit_Carry_Lookahead_Adder u_16_bit_carry_lookahead_adder_1 (
    .a(a[31:16]), .b(b[31:16]), .C0(n16_bit_carry_lookahead_adder_2_c16), .S(S[31:16]), .C16(C32), .C15(C31));  // open: G, P
  _16_bit_Carry_Lookahead_Adder u_16_bit_carry_lookahead_adder_2 (
    .a(a[15:0]), .b(b[15:0]), .C0(C0), .S(S[15:0]), .C16(n16_bit_carry_lookahead_adder_2_c16));  // open: G, P, C15
  // Probe on a
  // Probe on b
  // Probe on S
  // Probe on a
  // Probe on b
  // Probe on S

  // Other names for the same wires on the sheet: a0[15:0] = a[15:0]; a1[15:0] = a[31:16]; b0[15:0] = b[15:0];
  //   b1[15:0] = b[31:16]; S0[15:0] = S[15:0]; S1[15:0] = S[31:16]

  // Notes on the sheet:
  //   Input
  //   Note: Please reference the lecture slides to understand the meaning of inputs and outputs.
  //   Output
  //   +
  //   =
  //   Unsigned Result
  //   +
  //   =
  //   Signed Result
endmodule

module _32_bit_ALU (
  input  [3:0] ALUOp,
  input  [31:0] a,
  input  [31:0] b,
  output Overflow,
  output Zero,
  output [31:0] Result
);

  wire n32_bit_carry_lookahead_adder_1_c31, n32_bit_carry_lookahead_adder_1_c32;
  wire [31:0] and_1_out, multiplexer_1_out, multiplexer_2_out, n32_bit_carry_lookahead_adder_1_s, not_1_out,
       not_2_out, or_1_out;

  assign not_1_out = ~a;  // NOT_Gate not_1, 32 bits wide
  assign not_2_out = ~b;  // NOT_Gate not_2, 32 bits wide
  xor xor_1 (Overflow, n32_bit_carry_lookahead_adder_1_c32, n32_bit_carry_lookahead_adder_1_c31);
  Multiplexer #(.width(32), .enable("false")) multiplexer_1 (
    .in0(a), .in1(not_1_out), .out(multiplexer_1_out), .sel(ALUOp[3]));
  Multiplexer #(.width(32), .enable("false")) multiplexer_2 (
    .in0(b), .in1(not_2_out), .out(multiplexer_2_out), .sel(ALUOp[2]));
  assign and_1_out = multiplexer_1_out & multiplexer_2_out;  // AND_Gate and_1, 32 bits wide
  assign or_1_out = multiplexer_1_out | multiplexer_2_out;  // OR_Gate or_1, 32 bits wide
  Multiplexer #(.select(2), .width(32), .enable("false")) multiplexer_3 (
    .in0(and_1_out), .in1(or_1_out), .in2(n32_bit_carry_lookahead_adder_1_s), .in3(b), .out(Result),
    .sel(ALUOp[1:0]));
  _32_bit_Carry_Lookahead_Adder u_32_bit_carry_lookahead_adder_1 (
    .a(multiplexer_1_out), .b(multiplexer_2_out), .C0(ALUOp[2]), .S(n32_bit_carry_lookahead_adder_1_s),
    .C32(n32_bit_carry_lookahead_adder_1_c32), .C31(n32_bit_carry_lookahead_adder_1_c31));
  nor nor_1 (Zero, Result[16], Result[31], Result[30], Result[29], Result[28], Result[27], Result[26], Result[25], Result[24], Result[23], Result[22], Result[21], Result[20], Result[19], Result[18], Result[17], Result[15], Result[14], Result[13], Result[12], Result[11], Result[10], Result[9], Result[8], Result[7], Result[6], Result[5], Result[4], Result[3], Result[2], Result[1], Result[0]);

  // Other names for the same wires on the sheet: Operation[1:0] = ALUOp[1:0]; Binvert = ALUOp[2]; Ainvert = ALUOp[3]

  // Notes on the sheet:
  //   Input
  //   Function: 32-bit AND, OR, Add, Subtract, Set on less than, NOR. For details please reference lab instruction. 
  //   Output
endmodule

module _8_bit_Multiplication__Version_1 (
  input  [7:0] Multiplicand,
  input  [7:0] Multiplier,
  output [15:0] Product
);

  wire Clock_out, comparator_1_eq, comparator_2_lt, not_1_out, Reset;
  wire [7:0] Counter_q, multiplexer_2_out, Multiplier_q, shifter_2_out;
  wire [15:0] bit_extender_1_out, multiplexer_1_out, multiplexer_3_out, Multiplicand_q,
       n16_bit_carry_lookahead_adder_1_s, shifter_1_out;

  assign bit_extender_1_out = {{8{1'b0}}, Multiplicand};  // Bit_Extender bit_extender_1
  Shifter #(.width(16)) shifter_1 (.in(Multiplicand_q), .\dist (4'b0001), .out(shifter_1_out));
  Shifter #(.shift("lr")) shifter_2 (.in(Multiplier_q), .\dist (3'b001), .out(shifter_2_out));
  Multiplexer #(.width(16), .enable("false")) multiplexer_1 (
    .in0(bit_extender_1_out), .in1(shifter_1_out), .out(multiplexer_1_out), .sel(not_1_out));
  Multiplexer #(.width(8), .enable("false")) multiplexer_2 (
    .in0(Multiplier), .in1(shifter_2_out), .out(multiplexer_2_out), .sel(not_1_out));
  _16_bit_Carry_Lookahead_Adder u_16_bit_carry_lookahead_adder_1 (
    .a(multiplexer_3_out), .b(Product), .C0(1'b0), .S(n16_bit_carry_lookahead_adder_1_s));  // open: C16, G, P, C15
  Register #(.width(16)) u_Multiplicand (
    .D(multiplexer_1_out), .en(comparator_2_lt), .Q(Multiplicand_q), .clk(Clock_out), .clr(Reset));
  Register u_Multiplier (.D(multiplexer_2_out), .en(comparator_2_lt), .Q(Multiplier_q), .clk(Clock_out), .clr(Reset));
  Multiplexer #(.width(16), .enable("false")) multiplexer_3 (
    .in0({16{1'b0}}), .in1(Multiplicand_q), .out(multiplexer_3_out), .sel(Multiplier_q[0]));
  Counter Counter (.count(comparator_2_lt), .Q(Counter_q), .clk(Clock_out), .clr(Reset));  // open: load, D, carry
  Button u_Reset (.out(Reset));
  Comparator comparator_1 (.a({8{1'b0}}), .b(Counter_q), .eq(comparator_1_eq));  // open: gt, lt
  not not_1 (not_1_out, comparator_1_eq);
  Comparator comparator_2 (.a(Counter_q), .b(8'h8), .lt(comparator_2_lt));  // open: gt, eq
  Register #(.width(16)) u_Product (
    .D(n16_bit_carry_lookahead_adder_1_s), .Q(Product), .clk(Clock_out), .clr(Reset));  // open: en
  Clock Clock (.out(Clock_out));
  // Probe on Multiplicand
  // Probe on Multiplier
  // Probe on Product

  // Notes on the sheet:
  //   Input
  //   Output
  //   x
  //   =
endmodule

module _8_bit_Multiplication__Refined_Version (
  input  [7:0] Multiplicand,
  input  [7:0] Multiplier,
  output [15:0] Product
);

  wire Clock_out, comparator_1_eq, comparator_2_eq, comparator_3_lt, not_1_out, not_2_out, Reset;
  wire [7:0] Counter_q, multiplexer_1_out, multiplexer_2_out, multiplexer_3_out,
       n8_bit_ripple_carry_adder_and_subtracter_1_s, Product1_q, Product2_q;
  wire [15:0] shifter_1_out;

  _8_bit_Ripple_Carry_Adder_and_Subtracter u_8_bit_ripple_carry_adder_and_subtracter_1 (
    .a(multiplexer_1_out), .b(Product[15:8]), .Sub(1'b0), .S(n8_bit_ripple_carry_adder_and_subtracter_1_s));  // open: CarryOut, Overflow
  Multiplexer #(.width(8), .enable("false")) multiplexer_1 (
    .in0({8{1'b0}}), .in1(Multiplicand), .out(multiplexer_1_out), .sel(Product[0]));
  Multiplexer #(.width(8), .enable("false")) multiplexer_2 (
    .in0(Multiplier), .in1(Product[7:0]), .out(multiplexer_2_out), .sel(not_2_out));
  Clock Clock (.out(Clock_out));
  Button u_Reset (.out(Reset));
  Register Product1 (.D(multiplexer_3_out), .en(comparator_3_lt), .Q(Product1_q), .clk(Clock_out), .clr(Reset));
  Multiplexer #(.width(8), .enable("false")) multiplexer_3 (
    .in0({8{1'b0}}), .in1(n8_bit_ripple_carry_adder_and_subtracter_1_s), .out(multiplexer_3_out),
    .sel(not_2_out));
  Register Product2 (.D(multiplexer_2_out), .en(comparator_3_lt), .Q(Product2_q), .clk(Clock_out), .clr(Reset));
  Counter Counter (.count(comparator_3_lt), .Q(Counter_q), .clk(Clock_out), .clr(Reset));  // open: load, D, carry
  Multiplexer #(.width(16), .enable("false")) multiplexer_4 (
    .in0({Product1_q, Product2_q}), .in1(shifter_1_out), .out(Product), .sel(not_1_out));
  Shifter #(.width(16), .shift("lr")) shifter_1 (.in({Product1_q, Product2_q}), .\dist (4'b0001), .out(shifter_1_out));
  Comparator comparator_1 (.a({8{1'b0}}), .b(Counter_q), .eq(comparator_1_eq));  // open: gt, lt
  not not_1 (not_1_out, comparator_2_eq);
  not not_2 (not_2_out, comparator_1_eq);
  Comparator comparator_2 (.a(8'h1), .b(Counter_q), .eq(comparator_2_eq));  // open: gt, lt
  Comparator comparator_3 (.a(Counter_q), .b(8'h9), .lt(comparator_3_lt));  // open: gt, eq
  // Probe on Multiplicand
  // Probe on Multiplier
  // Probe on Product

  // Notes on the sheet:
  //   Input
  //   Output
  //   x
  //   =
endmodule

module alu___copy (
  input  [3:0] ALUOp,
  input  [31:0] a,
  input  [31:0] b,
  output Overflow,
  output Zero,
  output [31:0] Result
);

  wire comparator_1_lt, n32_bit_carry_lookahead_adder_1_c31, n32_bit_carry_lookahead_adder_1_c32;
  wire [31:0] and_1_out, bit_extender_1_out, multiplexer_1_out, multiplexer_2_out,
       n32_bit_carry_lookahead_adder_1_s, not_1_out, not_2_out, or_1_out;

  Comparator #(.width(32)) comparator_1 (.a(a), .b(b), .lt(comparator_1_lt));  // open: gt, eq
  assign not_1_out = ~a;  // NOT_Gate not_1, 32 bits wide
  assign not_2_out = ~b;  // NOT_Gate not_2, 32 bits wide
  assign bit_extender_1_out = {{31{1'b0}}, comparator_1_lt};  // Bit_Extender bit_extender_1
  xor xor_1 (Overflow, n32_bit_carry_lookahead_adder_1_c32, n32_bit_carry_lookahead_adder_1_c31);
  Multiplexer #(.width(32), .enable("false")) multiplexer_1 (
    .in0(a), .in1(not_1_out), .out(multiplexer_1_out), .sel(ALUOp[3]));
  Multiplexer #(.width(32), .enable("false")) multiplexer_2 (
    .in0(b), .in1(not_2_out), .out(multiplexer_2_out), .sel(ALUOp[2]));
  assign and_1_out = multiplexer_1_out & multiplexer_2_out;  // AND_Gate and_1, 32 bits wide
  assign or_1_out = multiplexer_1_out | multiplexer_2_out;  // OR_Gate or_1, 32 bits wide
  Multiplexer #(.select(2), .width(32), .enable("false")) multiplexer_3 (
    .in0(and_1_out), .in1(or_1_out), .in2(n32_bit_carry_lookahead_adder_1_s), .in3(bit_extender_1_out),
    .out(Result), .sel(ALUOp[1:0]));
  _32_bit_Carry_Lookahead_Adder u_32_bit_carry_lookahead_adder_1 (
    .a(multiplexer_1_out), .b(multiplexer_2_out), .C0(ALUOp[2]), .S(n32_bit_carry_lookahead_adder_1_s),
    .C32(n32_bit_carry_lookahead_adder_1_c32), .C31(n32_bit_carry_lookahead_adder_1_c31));
  nor nor_1 (Zero, Result[16], Result[31], Result[30], Result[29], Result[28], Result[27], Result[26], Result[25], Result[24], Result[23], Result[22], Result[21], Result[20], Result[19], Result[18], Result[17], Result[15], Result[14], Result[13], Result[12], Result[11], Result[10], Result[9], Result[8], Result[7], Result[6], Result[5], Result[4], Result[3], Result[2], Result[1], Result[0]);

  // Other names for the same wires on the sheet: Operation[1:0] = ALUOp[1:0]; Binvert = ALUOp[2]; Ainvert = ALUOp[3]

  // Notes on the sheet:
  //   Input
  //   Function: 32-bit AND, OR, Add, Subtract, Set on less than, NOR. For details please reference lab instruction. 
  //   Output
endmodule
