// Logisim project circuit.circ as structural Verilog: 4 circuits, main circuit 3bit ADC
module _3bit_ADC (
  input  in_1,
  output out_2,
  output out_3,
  output out_4
);

  wire and_1_out, and_2_out, and_3_out, and_4_out, and_5_out, and_6_out, and_7_out, and_8_out, and_9_out,
       and_10_out, and_11_out, and_12_out, and_13_out, and_14_out, not_1_out, not_2_out, not_3_out,
       not_4_out, not_5_out, not_6_out, not_7_out, not_8_out, not_9_out, not_10_out, not_11_out, not_12_out,
       not_13_out, not_14_out, not_15_out, not_16_out, not_17_out, not_18_out, not_19_out, not_20_out,
       not_21_out, or_1_out, or_2_out, or_3_out, or_4_out, or_5_out, or_6_out, or_7_out,
       pull_resistor_1_node, pull_resistor_2_node, pull_resistor_3_node, pull_resistor_4_node,
       pull_resistor_5_node, pull_resistor_6_node, pull_resistor_7_node, pull_resistor_8_node;

  Pull_Resistor #(.pull(1)) pull_resistor_1 (.node(pull_resistor_1_node));
  Pull_Resistor #(.pull(1)) pull_resistor_2 (.node(pull_resistor_2_node));
  Pull_Resistor #(.pull(1)) pull_resistor_3 (.node(pull_resistor_3_node));
  Pull_Resistor #(.pull(1)) pull_resistor_4 (.node(pull_resistor_4_node));
  Pull_Resistor #(.pull(1)) pull_resistor_5 (.node(pull_resistor_5_node));
  Pull_Resistor #(.pull(1)) pull_resistor_6 (.node(pull_resistor_6_node));
  Pull_Resistor #(.pull(1)) pull_resistor_7 (.node(pull_resistor_7_node));
  not not_1 (not_1_out, in_1);
  and and_1 (and_1_out, not_1_out, 1'b1);
  and and_2 (and_2_out, in_1, not_2_out);
  not not_2 (not_2_out, 1'b1);
  not not_3 (not_3_out, in_1);
  and and_3 (and_3_out, not_3_out, pull_resistor_1_node);
  and and_4 (and_4_out, in_1, not_4_out);
  not not_4 (not_4_out, pull_resistor_1_node);
  not not_5 (not_5_out, in_1);
  and and_5 (and_5_out, not_5_out, pull_resistor_2_node);
  and and_6 (and_6_out, in_1, not_6_out);
  not not_6 (not_6_out, pull_resistor_2_node);
  not not_7 (not_7_out, in_1);
  and and_7 (and_7_out, not_7_out, pull_resistor_3_node);
  and and_8 (and_8_out, in_1, not_8_out);
  not not_8 (not_8_out, pull_resistor_3_node);
  not not_9 (not_9_out, in_1);
  and and_9 (and_9_out, not_9_out, pull_resistor_4_node);
  and and_10 (and_10_out, in_1, not_10_out);
  not not_10 (not_10_out, pull_resistor_4_node);
  not not_11 (not_11_out, in_1);
  and and_11 (and_11_out, not_11_out, pull_resistor_5_node);
  and and_12 (and_12_out, in_1, not_12_out);
  not not_12 (not_12_out, pull_resistor_5_node);
  not not_13 (not_13_out, in_1);
  and and_13 (and_13_out, not_13_out, pull_resistor_6_node);
  and and_14 (and_14_out, in_1, not_14_out);
  not not_14 (not_14_out, pull_resistor_6_node);
  or or_1 (or_1_out, and_1_out, and_2_out);
  not not_15 (not_15_out, or_1_out);
  or or_2 (or_2_out, and_3_out, and_4_out);
  not not_16 (not_16_out, or_2_out);
  or or_3 (or_3_out, and_5_out, and_6_out);
  not not_17 (not_17_out, or_3_out);
  not not_18 (not_18_out, or_4_out);
  or or_4 (or_4_out, and_7_out, and_8_out);
  or or_5 (or_5_out, and_9_out, and_10_out);
  not not_19 (not_19_out, or_5_out);
  or or_6 (or_6_out, and_11_out, and_12_out);
  not not_20 (not_20_out, or_6_out);
  not not_21 (not_21_out, or_7_out);
  or or_7 (or_7_out, and_13_out, and_14_out);
  xor xor_1 (out_2, 1'b0, and_1_out);
  xor xor_2 (out_2, and_2_out, and_3_out);
  xor xor_3 (out_2, and_4_out, and_5_out);
  xor xor_4 (out_2, and_6_out, and_7_out);
  xor xor_5 (out_2, and_8_out, and_9_out);
  xor xor_6 (out_2, and_10_out, and_11_out);
  xor xor_7 (out_2, and_12_out, and_13_out);
  Pull_Resistor pull_resistor_8 (.node(pull_resistor_8_node));
  Pull_Resistor pull_resistor_9 (.node(pull_resistor_8_node));
  Pull_Resistor pull_resistor_10 (.node(pull_resistor_8_node));

  assign out_3 = out_2;
  assign out_4 = out_2;
  // also tied to GND on the sheet: {pull_resistor_7_node, pull_resistor_8_node}
endmodule

module cmos_ADC (
  input  in_1,
  input  in_2
);

  wire pull_resistor_1_node, pull_resistor_2_node, pull_resistor_3_node, pull_resistor_4_node,
       pull_resistor_5_node, pull_resistor_6_node, pull_resistor_7_node, transistor_1_out, transistor_2_out,
       transistor_3_out, transistor_4_out, transistor_5_out, transistor_6_out, transistor_7_out,
       transistor_8_out, transistor_9_out, transistor_10_out, transistor_11_out, transistor_13_out,
       transistor_14_out, transistor_15_out, transistor_16_out, transistor_17_out, transistor_18_out,
       transistor_19_out, transistor_21_out, transistor_23_out, transistor_25_out, transistor_26_out,
       transistor_27_out, transistor_28_out, transistor_29_out, transistor_30_out, transistor_31_out,
       transistor_32_out, transistor_33_out, transistor_34_out, transistor_35_out, transistor_36_out,
       transistor_37_out, transistor_38_out, transistor_39_out, transistor_40_out, transistor_41_out,
       transistor_42_out, transistor_43_out, transistor_44_out, transistor_45_out, transistor_46_out,
       transistor_47_out, transistor_48_out, transistor_49_out, transistor_50_out, transistor_51_out,
       transistor_52_out, transistor_53_out, transistor_54_out, transistor_55_out, transistor_56_out,
       transistor_57_out, transistor_58_out, transistor_59_out, transistor_60_out, transistor_61_out,
       transistor_62_out, transistor_63_out, transistor_65_out, transistor_66_out, transistor_67_out,
       transistor_68_out, transistor_69_out, transistor_70_out, transistor_71_out, transistor_72_out,
       transistor_73_out, transistor_74_out, transistor_75_out, transistor_76_out, transistor_77_out,
       transistor_78_out, transistor_79_out, transistor_80_out, transistor_81_out, transistor_82_out,
       transistor_84_out, transistor_85_out, transistor_87_out, transistor_88_out, transistor_89_out,
       transistor_90_out, transistor_91_out, transistor_92_out, transistor_93_out, transistor_94_out,
       transistor_95_out, transistor_96_out, transistor_97_out, transistor_98_out, transistor_99_out,
       transistor_100_out, transistor_101_out, transistor_102_out, transistor_103_out, transistor_104_out,
       transistor_105_out, transistor_106_out, transistor_107_out, transistor_121_out, transistor_123_out,
       transistor_124_out, transistor_125_out, transistor_126_out, transistor_127_out, transistor_128_out,
       transistor_129_out, transistor_130_out, transistor_131_out, transistor_132_out, transistor_133_out,
       transistor_134_out, transistor_135_out, transistor_136_out, transistor_137_out, transistor_138_out,
       transistor_139_out, transistor_140_out, transistor_141_out, transistor_142_out, transistor_143_out,
       transistor_144_out, transistor_145_out, transistor_146_out, transistor_147_out, transistor_148_out,
       transistor_149_out, transistor_150_out, transistor_151_out, transistor_152_out, transistor_153_out,
       transistor_154_out, transistor_155_out, transistor_156_out, transistor_157_out, transistor_158_out,
       transistor_159_out, transistor_160_out, transistor_161_out, transistor_162_out, transistor_163_out,
       transistor_164_out, transistor_165_out, transistor_166_out, transistor_167_out, transistor_168_out,
       transistor_169_out, transistor_170_out, transistor_171_out, transistor_172_out, transistor_173_out,
       transistor_174_out, transistor_175_out, transistor_176_out, transistor_177_out, transistor_178_out,
       transistor_179_out, transistor_181_out, transistor_183_out, transistor_185_out, transistor_187_out,
       transistor_189_out, transistor_191_out, transistor_193_out, transistor_195_out, transistor_197_out,
       transistor_199_out, transistor_201_out, transistor_203_out, transistor_205_out, undriven, undriven_2,
       undriven_3, undriven_4, undriven_5, undriven_6, undriven_7, undriven_8, undriven_9, undriven_10,
       undriven_11, undriven_12, undriven_13, undriven_14, undriven_15, undriven_16, undriven_17,
       undriven_18, undriven_19, undriven_20, undriven_21, undriven_22, undriven_23, undriven_24,
       undriven_25, undriven_26, undriven_27, undriven_28, undriven_29, undriven_30;

  Pull_Resistor #(.pull(1)) pull_resistor_1 (.node(pull_resistor_1_node));
  Pull_Resistor #(.pull(1)) pull_resistor_2 (.node(pull_resistor_2_node));
  Pull_Resistor #(.pull(1)) pull_resistor_3 (.node(pull_resistor_3_node));
  Pull_Resistor #(.pull(1)) pull_resistor_4 (.node(pull_resistor_4_node));
  Pull_Resistor #(.pull(1)) pull_resistor_5 (.node(pull_resistor_5_node));
  Pull_Resistor #(.pull(1)) pull_resistor_6 (.node(pull_resistor_6_node));
  Pull_Resistor #(.pull(1)) pull_resistor_7 (.node(pull_resistor_7_node));
  Transistor #(.\type ("n")) transistor_1 (.in(transistor_11_out), .out(transistor_1_out), .gate(undriven));
  Transistor transistor_2 (.in(1'b1), .out(transistor_2_out), .gate(undriven_4));
  Transistor #(.\type ("n")) transistor_3 (.in(transistor_2_out), .out(transistor_3_out), .gate(undriven_4));
  Transistor transistor_4 (.in(1'b1), .out(transistor_4_out), .gate(undriven_4));
  Transistor transistor_5 (.in(transistor_4_out), .out(transistor_5_out), .gate(transistor_8_out));
  Transistor #(.\type ("n")) transistor_6 (.in(transistor_5_out), .out(transistor_6_out), .gate(undriven_4));
  Transistor #(.\type ("n")) transistor_7 (.in(transistor_6_out), .out(transistor_7_out), .gate(undriven_6));
  Transistor transistor_8 (.in(1'b1), .out(transistor_8_out), .gate(undriven_6));
  Transistor #(.\type ("n")) transistor_9 (.in(transistor_8_out), .out(transistor_9_out), .gate(undriven_6));
  Transistor transistor_10 (.in(1'b1), .out(transistor_10_out), .gate(undriven));
  Transistor transistor_11 (.in(transistor_10_out), .out(transistor_11_out), .gate(undriven_5));
  Transistor #(.\type ("n")) transistor_12 (.in(transistor_11_out), .out(transistor_1_out), .gate(undriven_5));
  Transistor transistor_13 (.in(1'b1), .out(transistor_13_out), .gate(undriven_2));
  Transistor #(.\type ("n")) transistor_14 (.in(transistor_13_out), .out(transistor_14_out), .gate(undriven_2));
  Transistor transistor_15 (.in(1'b1), .out(transistor_15_out), .gate(transistor_16_out));
  Transistor transistor_16 (.in(1'b1), .out(transistor_16_out), .gate(undriven_3));
  Transistor #(.\type ("n")) transistor_17 (.in(transistor_16_out), .out(transistor_17_out), .gate(undriven_3));
  Transistor #(.\type ("n")) transistor_18 (.in(transistor_15_out), .out(transistor_18_out), .gate(transistor_16_out));
  Transistor transistor_19 (.in(1'b1), .out(transistor_19_out), .gate(transistor_2_out));
  Transistor transistor_20 (.in(transistor_19_out), .out(transistor_5_out), .gate(undriven_6));
  Transistor #(.\type ("n")) transistor_21 (.in(transistor_5_out), .out(transistor_21_out), .gate(transistor_2_out));
  Transistor #(.\type ("n")) transistor_22 (.in(transistor_21_out), .out(transistor_7_out), .gate(undriven_6));
  Transistor transistor_23 (.in(1'b1), .out(transistor_23_out), .gate(undriven_7));
  Transistor transistor_24 (.in(1'b1), .out(transistor_23_out), .gate(undriven_8));
  Transistor #(.\type ("n")) transistor_25 (.in(transistor_23_out), .out(transistor_25_out), .gate(undriven_8));
  Transistor #(.\type ("n")) transistor_26 (.in(transistor_25_out), .out(transistor_26_out), .gate(undriven_7));
  Transistor transistor_27 (.in(1'b1), .out(transistor_27_out), .gate(in_2));
  Transistor #(.\type ("n")) transistor_28 (.in(transistor_27_out), .out(transistor_28_out), .gate(in_2));
  Transistor transistor_29 (.in(1'b1), .out(transistor_29_out), .gate(undriven_10));
  Transistor #(.\type ("n")) transistor_30 (.in(transistor_29_out), .out(transistor_30_out), .gate(undriven_10));
  Transistor transistor_31 (.in(1'b1), .out(transistor_31_out), .gate(in_2));
  Transistor #(.\type ("n")) transistor_32 (.in(transistor_31_out), .out(transistor_32_out), .gate(in_2));
  Transistor transistor_33 (.in(1'b1), .out(transistor_33_out), .gate(undriven_12));
  Transistor #(.\type ("n")) transistor_34 (.in(transistor_33_out), .out(transistor_34_out), .gate(undriven_12));
  Transistor transistor_35 (.in(1'b1), .out(transistor_35_out), .gate(in_2));
  Transistor #(.\type ("n")) transistor_36 (.in(transistor_35_out), .out(transistor_36_out), .gate(in_2));
  Transistor transistor_37 (.in(1'b1), .out(transistor_37_out), .gate(undriven_13));
  Transistor #(.\type ("n")) transistor_38 (.in(transistor_37_out), .out(transistor_38_out), .gate(undriven_13));
  Transistor transistor_39 (.in(1'b1), .out(transistor_39_out), .gate(in_2));
  Transistor transistor_40 (.in(1'b1), .out(transistor_40_out), .gate(undriven_11));
  Transistor #(.\type ("n")) transistor_41 (.in(transistor_39_out), .out(transistor_41_out), .gate(in_2));
  Transistor transistor_42 (.in(1'b1), .out(transistor_42_out), .gate(transistor_43_out));
  Transistor transistor_43 (.in(1'b1), .out(transistor_43_out), .gate(undriven_11));
  Transistor #(.\type ("n")) transistor_44 (.in(transistor_43_out), .out(transistor_44_out), .gate(undriven_11));
  Transistor transistor_45 (.in(1'b1), .out(transistor_45_out), .gate(in_2));
  Transistor #(.\type ("n")) transistor_46 (.in(transistor_45_out), .out(transistor_46_out), .gate(in_2));
  Transistor transistor_47 (.in(1'b1), .out(transistor_47_out), .gate(undriven_9));
  Transistor #(.\type ("n")) transistor_48 (.in(transistor_47_out), .out(transistor_48_out), .gate(undriven_9));
  Transistor transistor_49 (.in(1'b1), .out(transistor_49_out), .gate(in_2));
  Transistor #(.\type ("n")) transistor_50 (.in(transistor_49_out), .out(transistor_50_out), .gate(in_2));
  Transistor transistor_51 (.in(1'b1), .out(transistor_51_out), .gate(undriven_14));
  Transistor #(.\type ("n")) transistor_52 (.in(transistor_51_out), .out(transistor_52_out), .gate(undriven_14));
  Transistor transistor_53 (.in(1'b1), .out(transistor_53_out), .gate(in_2));
  Transistor #(.\type ("n")) transistor_54 (.in(transistor_53_out), .out(transistor_54_out), .gate(in_2));
  Transistor transistor_55 (.in(1'b1), .out(transistor_55_out), .gate(undriven_15));
  Transistor #(.\type ("n")) transistor_56 (.in(transistor_55_out), .out(transistor_56_out), .gate(undriven_15));
  Transistor #(.\type ("n")) transistor_57 (.in(1'b1), .out(transistor_57_out), .gate(1'b1));
  Transistor #(.\type ("n")) transistor_58 (.in(1'b1), .out(transistor_58_out), .gate(1'b1));
  Transistor transistor_59 (.in(transistor_58_out), .out(transistor_59_out), .gate(undriven_16));
  Transistor transistor_60 (.in(transistor_57_out), .out(transistor_60_out), .gate(transistor_59_out));
  Transistor #(.\type ("n")) transistor_61 (.in(transistor_59_out), .out(transistor_61_out), .gate(undriven_16));
  Transistor #(.\type ("n")) transistor_62 (.in(transistor_60_out), .out(transistor_62_out), .gate(transistor_59_out));
  Transistor transistor_63 (.in(transistor_62_out), .out(transistor_63_out), .gate(transistor_63_out));
  Transistor transistor_64 (.in(transistor_61_out), .out(transistor_63_out), .gate(transistor_63_out));
  Transistor transistor_65 (.in(1'b1), .out(transistor_65_out), .gate(undriven_10));
  Transistor #(.\type ("n")) transistor_66 (.in(transistor_65_out), .out(transistor_66_out), .gate(transistor_27_out));
  Transistor #(.\type ("n")) transistor_67 (.in(transistor_66_out), .out(transistor_67_out), .gate(undriven_10));
  Transistor transistor_68 (.in(1'b1), .out(transistor_68_out), .gate(transistor_29_out));
  Transistor #(.\type ("n")) transistor_69 (.in(transistor_68_out), .out(transistor_69_out), .gate(in_2));
  Transistor #(.\type ("n")) transistor_70 (.in(transistor_69_out), .out(transistor_70_out), .gate(transistor_29_out));
  Transistor transistor_71 (.in(1'b1), .out(transistor_71_out), .gate(undriven_12));
  Transistor #(.\type ("n")) transistor_72 (.in(transistor_71_out), .out(transistor_72_out), .gate(transistor_31_out));
  Transistor #(.\type ("n")) transistor_73 (.in(transistor_72_out), .out(transistor_73_out), .gate(undriven_12));
  Transistor transistor_74 (.in(1'b1), .out(transistor_74_out), .gate(transistor_33_out));
  Transistor #(.\type ("n")) transistor_75 (.in(transistor_74_out), .out(transistor_75_out), .gate(in_2));
  Transistor #(.\type ("n")) transistor_76 (.in(transistor_75_out), .out(transistor_76_out), .gate(transistor_33_out));
  Transistor transistor_77 (.in(1'b1), .out(transistor_77_out), .gate(undriven_13));
  Transistor #(.\type ("n")) transistor_78 (.in(transistor_77_out), .out(transistor_78_out), .gate(transistor_35_out));
  Transistor #(.\type ("n")) transistor_79 (.in(transistor_78_out), .out(transistor_79_out), .gate(undriven_13));
  Transistor transistor_80 (.in(1'b1), .out(transistor_80_out), .gate(transistor_37_out));
  Transistor #(.\type ("n")) transistor_81 (.in(transistor_80_out), .out(transistor_81_out), .gate(in_2));
  Transistor #(.\type ("n")) transistor_82 (.in(transistor_81_out), .out(transistor_82_out), .gate(transistor_37_out));
  Transistor transistor_83 (.in(1'b1), .out(transistor_40_out), .gate(transistor_39_out));
  Transistor #(.\type ("n")) transistor_84 (.in(transistor_40_out), .out(transistor_84_out), .gate(transistor_39_out));
  Transistor #(.\type ("n")) transistor_85 (.in(transistor_84_out), .out(transistor_85_out), .gate(undriven_11));
  Transistor transistor_86 (.in(1'b1), .out(transistor_42_out), .gate(in_2));
  Transistor #(.\type ("n")) transistor_87 (.in(transistor_42_out), .out(transistor_87_out), .gate(in_2));
  Transistor #(.\type ("n")) transistor_88 (.in(transistor_87_out), .out(transistor_88_out), .gate(transistor_43_out));
  Transistor transistor_89 (.in(1'b1), .out(transistor_89_out), .gate(undriven_9));
  Transistor #(.\type ("n")) transistor_90 (.in(transistor_89_out), .out(transistor_90_out), .gate(transistor_45_out));
  Transistor #(.\type ("n")) transistor_91 (.in(transistor_90_out), .out(transistor_91_out), .gate(undriven_9));
  Transistor transistor_92 (.in(1'b1), .out(transistor_92_out), .gate(transistor_47_out));
  Transistor #(.\type ("n")) transistor_93 (.in(transistor_92_out), .out(transistor_93_out), .gate(in_2));
  Transistor #(.\type ("n")) transistor_94 (.in(transistor_93_out), .out(transistor_94_out), .gate(transistor_47_out));
  Transistor transistor_95 (.in(1'b1), .out(transistor_95_out), .gate(undriven_14));
  Transistor #(.\type ("n")) transistor_96 (.in(transistor_95_out), .out(transistor_96_out), .gate(transistor_49_out));
  Transistor #(.\type ("n")) transistor_97 (.in(transistor_96_out), .out(transistor_97_out), .gate(undriven_14));
  Transistor transistor_98 (.in(1'b1), .out(transistor_98_out), .gate(transistor_51_out));
  Transistor #(.\type ("n")) transistor_99 (.in(transistor_98_out), .out(transistor_99_out), .gate(in_2));
  Transistor #(.\type ("n")) transistor_100 (
    .in(transistor_99_out), .out(transistor_100_out), .gate(transistor_51_out));
  Transistor transistor_101 (.in(1'b1), .out(transistor_101_out), .gate(undriven_15));
  Transistor #(.\type ("n")) transistor_102 (
    .in(transistor_101_out), .out(transistor_102_out), .gate(transistor_53_out));
  Transistor #(.\type ("n")) transistor_103 (.in(transistor_102_out), .out(transistor_103_out), .gate(undriven_15));
  Transistor transistor_104 (.in(1'b1), .out(transistor_104_out), .gate(transistor_55_out));
  Transistor #(.\type ("n")) transistor_105 (.in(transistor_104_out), .out(transistor_105_out), .gate(in_2));
  Transistor #(.\type ("n")) transistor_106 (
    .in(transistor_105_out), .out(transistor_106_out), .gate(transistor_55_out));
  Transistor transistor_107 (.in(1'b1), .out(transistor_107_out), .gate(transistor_60_out));
  Transistor #(.\type ("n")) transistor_108 (
    .in(transistor_107_out), .out(transistor_63_out), .gate(transistor_60_out));
  Transistor transistor_109 (.in(1'b1), .out(transistor_65_out), .gate(transistor_27_out));
  Transistor transistor_110 (.in(1'b1), .out(transistor_68_out), .gate(in_2));
  Transistor transistor_111 (.in(1'b1), .out(transistor_71_out), .gate(transistor_31_out));
  Transistor transistor_112 (.in(1'b1), .out(transistor_74_out), .gate(in_2));
  Transistor transistor_113 (.in(1'b1), .out(transistor_77_out), .gate(transistor_35_out));
  Transistor transistor_114 (.in(1'b1), .out(transistor_80_out), .gate(in_2));
  Transistor transistor_115 (.in(1'b1), .out(transistor_89_out), .gate(transistor_45_out));
  Transistor transistor_116 (.in(1'b1), .out(transistor_92_out), .gate(in_2));
  Transistor transistor_117 (.in(1'b1), .out(transistor_95_out), .gate(transistor_49_out));
  Transistor transistor_118 (.in(1'b1), .out(transistor_98_out), .gate(in_2));
  Transistor transistor_119 (.in(1'b1), .out(transistor_101_out), .gate(transistor_53_out));
  Transistor transistor_120 (.in(1'b1), .out(transistor_104_out), .gate(in_2));
  Transistor transistor_121 (.in(1'b1), .out(transistor_121_out), .gate(transistor_107_out));
  Transistor #(.\type ("n")) transistor_122 (
    .in(transistor_121_out), .out(transistor_63_out), .gate(transistor_107_out));
  Transistor transistor_123 (.in(1'b1), .out(transistor_123_out), .gate(undriven_17));
  Transistor #(.\type ("n")) transistor_124 (.in(transistor_123_out), .out(transistor_124_out), .gate(undriven_17));
  Transistor transistor_125 (.in(1'b1), .out(transistor_125_out), .gate(undriven_17));
  Transistor transistor_126 (.in(transistor_125_out), .out(transistor_126_out), .gate(transistor_129_out));
  Transistor #(.\type ("n")) transistor_127 (.in(transistor_126_out), .out(transistor_127_out), .gate(undriven_17));
  Transistor #(.\type ("n")) transistor_128 (.in(transistor_127_out), .out(transistor_128_out), .gate(undriven_26));
  Transistor transistor_129 (.in(1'b1), .out(transistor_129_out), .gate(undriven_26));
  Transistor #(.\type ("n")) transistor_130 (.in(transistor_129_out), .out(transistor_130_out), .gate(undriven_26));
  Transistor transistor_131 (.in(1'b1), .out(transistor_131_out), .gate(undriven_18));
  Transistor #(.\type ("n")) transistor_132 (.in(transistor_131_out), .out(transistor_132_out), .gate(undriven_18));
  Transistor transistor_133 (.in(1'b1), .out(transistor_133_out), .gate(undriven_18));
  Transistor transistor_134 (.in(transistor_133_out), .out(transistor_134_out), .gate(transistor_137_out));
  Transistor #(.\type ("n")) transistor_135 (.in(transistor_134_out), .out(transistor_135_out), .gate(undriven_18));
  Transistor #(.\type ("n")) transistor_136 (.in(transistor_135_out), .out(transistor_136_out), .gate(undriven_27));
  Transistor transistor_137 (.in(1'b1), .out(transistor_137_out), .gate(undriven_27));
  Transistor #(.\type ("n")) transistor_138 (.in(transistor_137_out), .out(transistor_138_out), .gate(undriven_27));
  Transistor transistor_139 (.in(1'b1), .out(transistor_139_out), .gate(undriven_19));
  Transistor #(.\type ("n")) transistor_140 (.in(transistor_139_out), .out(transistor_140_out), .gate(undriven_19));
  Transistor transistor_141 (.in(1'b1), .out(transistor_141_out), .gate(undriven_19));
  Transistor transistor_142 (.in(transistor_141_out), .out(transistor_142_out), .gate(transistor_145_out));
  Transistor #(.\type ("n")) transistor_143 (.in(transistor_142_out), .out(transistor_143_out), .gate(undriven_19));
  Transistor #(.\type ("n")) transistor_144 (.in(transistor_143_out), .out(transistor_144_out), .gate(undriven_22));
  Transistor transistor_145 (.in(1'b1), .out(transistor_145_out), .gate(undriven_22));
  Transistor #(.\type ("n")) transistor_146 (.in(transistor_145_out), .out(transistor_146_out), .gate(undriven_22));
  Transistor transistor_147 (.in(1'b1), .out(transistor_147_out), .gate(undriven_23));
  Transistor #(.\type ("n")) transistor_148 (.in(transistor_147_out), .out(transistor_148_out), .gate(undriven_23));
  Transistor transistor_149 (.in(1'b1), .out(transistor_149_out), .gate(undriven_23));
  Transistor transistor_150 (.in(transistor_149_out), .out(transistor_150_out), .gate(transistor_153_out));
  Transistor #(.\type ("n")) transistor_151 (.in(transistor_150_out), .out(transistor_151_out), .gate(undriven_23));
  Transistor #(.\type ("n")) transistor_152 (.in(transistor_151_out), .out(transistor_152_out), .gate(undriven_28));
  Transistor transistor_153 (.in(1'b1), .out(transistor_153_out), .gate(undriven_28));
  Transistor #(.\type ("n")) transistor_154 (.in(transistor_153_out), .out(transistor_154_out), .gate(undriven_28));
  Transistor transistor_155 (.in(1'b1), .out(transistor_155_out), .gate(undriven_24));
  Transistor #(.\type ("n")) transistor_156 (.in(transistor_155_out), .out(transistor_156_out), .gate(undriven_24));
  Transistor transistor_157 (.in(1'b1), .out(transistor_157_out), .gate(undriven_24));
  Transistor transistor_158 (.in(transistor_157_out), .out(transistor_158_out), .gate(transistor_161_out));
  Transistor #(.\type ("n")) transistor_159 (.in(transistor_158_out), .out(transistor_159_out), .gate(undriven_24));
  Transistor #(.\type ("n")) transistor_160 (.in(transistor_159_out), .out(transistor_160_out), .gate(undriven_20));
  Transistor transistor_161 (.in(1'b1), .out(transistor_161_out), .gate(undriven_20));
  Transistor #(.\type ("n")) transistor_162 (.in(transistor_161_out), .out(transistor_162_out), .gate(undriven_20));
  Transistor transistor_163 (.in(1'b1), .out(transistor_163_out), .gate(undriven_25));
  Transistor #(.\type ("n")) transistor_164 (.in(transistor_163_out), .out(transistor_164_out), .gate(undriven_25));
  Transistor transistor_165 (.in(1'b1), .out(transistor_165_out), .gate(undriven_25));
  Transistor transistor_166 (.in(transistor_165_out), .out(transistor_166_out), .gate(transistor_169_out));
  Transistor #(.\type ("n")) transistor_167 (.in(transistor_166_out), .out(transistor_167_out), .gate(undriven_25));
  Transistor #(.\type ("n")) transistor_168 (.in(transistor_167_out), .out(transistor_168_out), .gate(undriven_29));
  Transistor transistor_169 (.in(1'b1), .out(transistor_169_out), .gate(undriven_29));
  Transistor #(.\type ("n")) transistor_170 (.in(transistor_169_out), .out(transistor_170_out), .gate(undriven_29));
  Transistor transistor_171 (.in(1'b1), .out(transistor_171_out), .gate(undriven_21));
  Transistor #(.\type ("n")) transistor_172 (.in(transistor_171_out), .out(transistor_172_out), .gate(undriven_21));
  Transistor transistor_173 (.in(1'b1), .out(transistor_173_out), .gate(undriven_21));
  Transistor transistor_174 (.in(transistor_173_out), .out(transistor_174_out), .gate(transistor_177_out));
  Transistor #(.\type ("n")) transistor_175 (.in(transistor_174_out), .out(transistor_175_out), .gate(undriven_21));
  Transistor #(.\type ("n")) transistor_176 (.in(transistor_175_out), .out(transistor_176_out), .gate(undriven_30));
  Transistor transistor_177 (.in(1'b1), .out(transistor_177_out), .gate(undriven_30));
  Transistor #(.\type ("n")) transistor_178 (.in(transistor_177_out), .out(transistor_178_out), .gate(undriven_30));
  Transistor transistor_179 (.in(1'b1), .out(transistor_179_out), .gate(transistor_123_out));
  Transistor transistor_180 (.in(transistor_179_out), .out(transistor_126_out), .gate(undriven_26));
  Transistor #(.\type ("n")) transistor_181 (
    .in(transistor_126_out), .out(transistor_181_out), .gate(transistor_123_out));
  Transistor #(.\type ("n")) transistor_182 (.in(transistor_181_out), .out(transistor_128_out), .gate(undriven_26));
  Transistor transistor_183 (.in(1'b1), .out(transistor_183_out), .gate(transistor_131_out));
  Transistor transistor_184 (.in(transistor_183_out), .out(transistor_134_out), .gate(undriven_27));
  Transistor #(.\type ("n")) transistor_185 (
    .in(transistor_134_out), .out(transistor_185_out), .gate(transistor_131_out));
  Transistor #(.\type ("n")) transistor_186 (.in(transistor_185_out), .out(transistor_136_out), .gate(undriven_27));
  Transistor transistor_187 (.in(1'b1), .out(transistor_187_out), .gate(transistor_139_out));
  Transistor transistor_188 (.in(transistor_187_out), .out(transistor_142_out), .gate(undriven_22));
  Transistor #(.\type ("n")) transistor_189 (
    .in(transistor_142_out), .out(transistor_189_out), .gate(transistor_139_out));
  Transistor #(.\type ("n")) transistor_190 (.in(transistor_189_out), .out(transistor_144_out), .gate(undriven_22));
  Transistor transistor_191 (.in(1'b1), .out(transistor_191_out), .gate(transistor_147_out));
  Transistor transistor_192 (.in(transistor_191_out), .out(transistor_150_out), .gate(undriven_28));
  Transistor #(.\type ("n")) transistor_193 (
    .in(transistor_150_out), .out(transistor_193_out), .gate(transistor_147_out));
  Transistor #(.\type ("n")) transistor_194 (.in(transistor_193_out), .out(transistor_152_out), .gate(undriven_28));
  Transistor transistor_195 (.in(1'b1), .out(transistor_195_out), .gate(transistor_155_out));
  Transistor transistor_196 (.in(transistor_195_out), .out(transistor_158_out), .gate(undriven_20));
  Transistor #(.\type ("n")) transistor_197 (
    .in(transistor_158_out), .out(transistor_197_out), .gate(transistor_155_out));
  Transistor #(.\type ("n")) transistor_198 (.in(transistor_197_out), .out(transistor_160_out), .gate(undriven_20));
  Transistor transistor_199 (.in(1'b1), .out(transistor_199_out), .gate(transistor_163_out));
  Transistor transistor_200 (.in(transistor_199_out), .out(transistor_166_out), .gate(undriven_29));
  Transistor #(.\type ("n")) transistor_201 (
    .in(transistor_166_out), .out(transistor_201_out), .gate(transistor_163_out));
  Transistor #(.\type ("n")) transistor_202 (.in(transistor_201_out), .out(transistor_168_out), .gate(undriven_29));
  Transistor transistor_203 (.in(1'b1), .out(transistor_203_out), .gate(transistor_171_out));
  Transistor transistor_204 (.in(transistor_203_out), .out(transistor_174_out), .gate(undriven_30));
  Transistor #(.\type ("n")) transistor_205 (
    .in(transistor_174_out), .out(transistor_205_out), .gate(transistor_171_out));
  Transistor #(.\type ("n")) transistor_206 (.in(transistor_205_out), .out(transistor_176_out), .gate(undriven_30));
  // also tied to GND on the sheet: {pull_resistor_7_node, transistor_1_out, transistor_14_out, transistor_17_out, transistor_3_out, transistor_9_out, transistor_7_out, transistor_18_out, transistor_26_out, transistor_41_out, transistor_44_out, transistor_32_out, transistor_34_out, transistor_36_out, transistor_38_out, transistor_46_out, transistor_48_out, transistor_50_out, transistor_52_out, transistor_54_out, transistor_56_out, transistor_28_out, transistor_30_out, transistor_63_out, transistor_85_out, transistor_88_out, transistor_73_out, transistor_76_out, transistor_79_out, transistor_82_out, transistor_91_out, transistor_94_out, transistor_97_out, transistor_100_out, transistor_103_out, transistor_106_out, transistor_67_out, transistor_70_out, transistor_124_out, transistor_130_out, transistor_132_out, transistor_138_out, transistor_140_out, transistor_146_out, transistor_148_out, transistor_154_out, transistor_156_out, transistor_162_out, transistor_164_out, transistor_170_out, transistor_172_out, transistor_178_out, transistor_136_out, transistor_144_out, transistor_152_out, transistor_176_out, transistor_128_out, transistor_160_out, transistor_168_out}
endmodule

module priority_encoder (
  input  in_1,
  input  in_2,
  input  in_3,
  input  in_4,
  input  in_5,
  input  in_6,
  input  in_7,
  output out_8,
  output out_9,
  output out_10
);

  wire and_1_out, and_2_out, and_3_out, and_4_out, not_1_out, not_2_out, not_3_out, not_4_out, not_5_out,
       not_6_out, not_7_out, not_8_out, not_9_out, not_10_out, not_11_out;

  not not_1 (not_1_out, in_1);
  not not_2 (not_2_out, in_3);
  not not_3 (not_3_out, in_2);
  not not_4 (not_4_out, not_2_out);
  not not_5 (not_5_out, not_3_out);
  and and_1 (and_1_out, not_5_out, not_2_out);
  nor nor_1 (out_8, not_1_out, not_3_out, not_6_out, and_1_out);
  not not_6 (not_6_out, in_4);
  not not_7 (not_7_out, in_5);
  not not_8 (not_8_out, not_6_out);
  and and_2 (and_2_out, not_5_out, not_4_out, not_8_out, not_7_out);
  nor nor_2 (out_9, and_2_out, not_1_out, not_3_out, and_4_out);
  not not_9 (not_9_out, in_6);
  not not_10 (not_10_out, in_7);
  not not_11 (not_11_out, not_9_out);
  and and_3 (and_3_out, not_4_out, not_10_out, not_8_out, not_11_out);
  and and_4 (and_4_out, not_9_out, not_4_out, not_8_out);
  nor nor_3 (out_10, not_1_out, and_1_out, and_2_out, and_3_out);
endmodule

module priority_encoder_cmos (
  input  in_1,
  input  in_2,
  input  in_3,
  input  in_4,
  input  in_5,
  input  in_6,
  input  in_7,
  output out_8,
  output out_9,
  output out_10
);

  wire transistor_1_out, transistor_2_out, transistor_3_out, transistor_4_out, transistor_5_out,
       transistor_6_out, transistor_7_out, transistor_8_out, transistor_9_out, transistor_10_out,
       transistor_11_out, transistor_12_out, transistor_13_out, transistor_14_out, transistor_15_out,
       transistor_16_out, transistor_17_out, transistor_18_out, transistor_19_out, transistor_20_out,
       transistor_21_out, transistor_22_out, transistor_23_out, transistor_25_out, transistor_26_out,
       transistor_27_out, transistor_29_out, transistor_30_out, transistor_31_out, transistor_32_out,
       transistor_33_out, transistor_35_out, transistor_36_out, transistor_37_out, transistor_38_out,
       transistor_40_out, transistor_41_out, transistor_42_out, transistor_43_out, transistor_49_out,
       transistor_50_out, transistor_52_out, transistor_53_out, transistor_54_out, transistor_56_out,
       transistor_57_out, transistor_58_out, transistor_60_out, transistor_67_out, transistor_68_out,
       undriven;

  Transistor transistor_1 (.in(1'b1), .out(transistor_1_out), .gate(in_1));
  Transistor #(.\type ("n")) transistor_2 (.in(transistor_1_out), .out(transistor_2_out), .gate(in_1));
  Transistor transistor_3 (.in(1'b1), .out(transistor_3_out), .gate(in_2));
  Transistor #(.\type ("n")) transistor_4 (.in(transistor_3_out), .out(transistor_4_out), .gate(in_2));
  Transistor transistor_5 (.in(1'b1), .out(transistor_5_out), .gate(in_3));
  Transistor #(.\type ("n")) transistor_6 (.in(transistor_5_out), .out(transistor_6_out), .gate(in_3));
  Transistor transistor_7 (.in(1'b1), .out(transistor_7_out), .gate(in_4));
  Transistor #(.\type ("n")) transistor_8 (.in(transistor_7_out), .out(transistor_8_out), .gate(in_4));
  Transistor transistor_9 (.in(1'b1), .out(transistor_9_out), .gate(in_5));
  Transistor #(.\type ("n")) transistor_10 (.in(transistor_9_out), .out(transistor_10_out), .gate(in_5));
  Transistor transistor_11 (.in(1'b1), .out(transistor_11_out), .gate(in_6));
  Transistor #(.\type ("n")) transistor_12 (.in(transistor_11_out), .out(transistor_12_out), .gate(in_6));
  Transistor transistor_13 (.in(1'b1), .out(transistor_13_out), .gate(in_7));
  Transistor #(.\type ("n")) transistor_14 (.in(transistor_13_out), .out(transistor_14_out), .gate(in_7));
  Transistor transistor_15 (.in(1'b1), .out(transistor_15_out), .gate(transistor_3_out));
  Transistor #(.\type ("n")) transistor_16 (.in(transistor_15_out), .out(transistor_16_out), .gate(transistor_3_out));
  Transistor transistor_17 (.in(1'b1), .out(transistor_17_out), .gate(transistor_5_out));
  Transistor #(.\type ("n")) transistor_18 (.in(transistor_17_out), .out(transistor_18_out), .gate(transistor_5_out));
  Transistor transistor_19 (.in(1'b1), .out(transistor_19_out), .gate(transistor_7_out));
  Transistor #(.\type ("n")) transistor_20 (.in(transistor_19_out), .out(transistor_20_out), .gate(transistor_7_out));
  Transistor transistor_21 (.in(1'b1), .out(transistor_21_out), .gate(transistor_11_out));
  Transistor #(.\type ("n")) transistor_22 (.in(transistor_21_out), .out(transistor_22_out), .gate(transistor_11_out));
  Transistor #(.gate("br")) transistor_23 (.in(1'b1), .out(transistor_23_out), .gate(transistor_5_out));
  Transistor transistor_24 (.in(1'b1), .out(transistor_23_out), .gate(transistor_15_out));
  Transistor #(.\type ("n")) transistor_25 (.in(transistor_23_out), .out(transistor_25_out), .gate(transistor_15_out));
  Transistor #(.\type ("n")) transistor_26 (.in(transistor_25_out), .out(transistor_26_out), .gate(transistor_5_out));
  Transistor transistor_27 (.in(1'b1), .out(transistor_27_out), .gate(transistor_17_out));
  Transistor #(.gate("br")) transistor_28 (.in(1'b1), .out(transistor_27_out), .gate(transistor_15_out));
  Transistor #(.\type ("n")) transistor_29 (.in(transistor_27_out), .out(transistor_29_out), .gate(transistor_17_out));
  Transistor #(.\type ("n")) transistor_30 (.in(transistor_29_out), .out(transistor_30_out), .gate(transistor_15_out));
  Transistor #(.\type ("n")) transistor_31 (.in(transistor_30_out), .out(transistor_31_out), .gate(transistor_9_out));
  Transistor #(.\type ("n")) transistor_32 (.in(transistor_31_out), .out(transistor_32_out), .gate(transistor_19_out));
  Transistor transistor_33 (.in(1'b1), .out(transistor_33_out), .gate(transistor_19_out));
  Transistor #(.gate("br")) transistor_34 (.in(1'b1), .out(transistor_33_out), .gate(transistor_15_out));
  Transistor #(.\type ("n")) transistor_35 (.in(transistor_33_out), .out(transistor_35_out), .gate(transistor_19_out));
  Transistor #(.\type ("n")) transistor_36 (.in(transistor_35_out), .out(transistor_36_out), .gate(transistor_15_out));
  Transistor #(.\type ("n")) transistor_37 (.in(transistor_36_out), .out(transistor_37_out), .gate(transistor_11_out));
  Transistor #(.gate("br")) transistor_38 (.in(1'b1), .out(transistor_38_out), .gate(transistor_15_out));
  Transistor transistor_39 (.in(1'b1), .out(transistor_38_out), .gate(transistor_21_out));
  Transistor #(.\type ("n")) transistor_40 (.in(transistor_38_out), .out(transistor_40_out), .gate(transistor_21_out));
  Transistor #(.\type ("n")) transistor_41 (.in(transistor_40_out), .out(transistor_41_out), .gate(transistor_15_out));
  Transistor #(.\type ("n")) transistor_42 (.in(transistor_41_out), .out(transistor_42_out), .gate(transistor_19_out));
  Transistor #(.\type ("n")) transistor_43 (.in(transistor_42_out), .out(transistor_43_out), .gate(transistor_13_out));
  Transistor #(.gate("br")) transistor_44 (.in(1'b1), .out(transistor_27_out), .gate(transistor_19_out));
  Transistor #(.gate("br")) transistor_45 (.in(1'b1), .out(transistor_27_out), .gate(transistor_9_out));
  Transistor #(.gate("br")) transistor_46 (.in(1'b1), .out(transistor_33_out), .gate(transistor_11_out));
  Transistor #(.gate("br")) transistor_47 (.in(1'b1), .out(transistor_38_out), .gate(transistor_13_out));
  Transistor #(.gate("br")) transistor_48 (.in(1'b1), .out(transistor_38_out), .gate(transistor_19_out));
  Transistor transistor_49 (.in(1'b1), .out(transistor_49_out), .gate(transistor_1_out));
  Transistor transistor_50 (.in(transistor_49_out), .out(transistor_50_out), .gate(transistor_3_out));
  Transistor transistor_51 (.in(transistor_50_out), .out(out_8), .gate(transistor_7_out));
  Transistor #(.\type ("n")) transistor_52 (.in(out_8), .out(transistor_52_out), .gate(transistor_7_out));
  Transistor transistor_53 (.in(1'b1), .out(transistor_53_out), .gate(transistor_1_out));
  Transistor transistor_54 (.in(transistor_53_out), .out(transistor_54_out), .gate(transistor_3_out));
  Transistor transistor_55 (.in(transistor_54_out), .out(out_9), .gate(transistor_33_out));
  Transistor #(.\type ("n")) transistor_56 (.in(out_9), .out(transistor_56_out), .gate(transistor_33_out));
  Transistor transistor_57 (.in(1'b1), .out(transistor_57_out), .gate(transistor_1_out));
  Transistor transistor_58 (.in(transistor_57_out), .out(transistor_58_out), .gate(transistor_27_out));
  Transistor transistor_59 (.in(transistor_58_out), .out(out_10), .gate(transistor_38_out));
  Transistor #(.\type ("n")) transistor_60 (.in(out_10), .out(transistor_60_out), .gate(transistor_38_out));
  Transistor #(.\type ("n"), .gate("br")) transistor_61 (.in(out_8), .out(transistor_52_out), .gate(transistor_3_out));
  Transistor #(.\type ("n"), .gate("br")) transistor_62 (.in(out_8), .out(transistor_52_out), .gate(transistor_1_out));
  Transistor #(.\type ("n"), .gate("br")) transistor_63 (.in(out_9), .out(transistor_56_out), .gate(transistor_1_out));
  Transistor #(.\type ("n"), .gate("br")) transistor_64 (.in(out_9), .out(transistor_56_out), .gate(transistor_3_out));
  Transistor #(.\type ("n"), .gate("br")) transistor_65 (.in(out_10), .out(transistor_60_out), .gate(transistor_1_out));
  Transistor #(.\type ("n"), .gate("br")) transistor_66 (
    .in(out_10), .out(transistor_60_out), .gate(transistor_27_out));
  Transistor transistor_67 (.in(1'b1), .out(transistor_67_out), .gate(undriven));
  Transistor #(.\type ("n")) transistor_68 (.in(transistor_67_out), .out(transistor_68_out), .gate(undriven));
  // also tied to GND on the sheet: {transistor_2_out, transistor_4_out, transistor_6_out, transistor_8_out, transistor_10_out, transistor_12_out, transistor_14_out, transistor_16_out, transistor_18_out, transistor_20_out, transistor_22_out, transistor_26_out, transistor_32_out, transistor_37_out, transistor_43_out, transistor_52_out, transistor_56_out, transistor_60_out, transistor_68_out}
endmodule
